// Logisim project logisimDesign1.circ as structural Verilog: 18 circuits, main circuit main
module main (
  input  in_1,
  input  [1:0] in_2,
  input  [11:0] in_3,
  input  in_4,
  input  [10:0] in_5,
  output out_6,
  output out_7
);

  wire alu_1_out_9, clock_1_out, control_unit_1_jump_imm_sel, control_unit_1_mem_load_enable,
       control_unit_1_mem_store_enable, control_unit_1_reg_load_enable, or_1_out;
  wire [3:0] control_unit_1_reg_no_dest, control_unit_1_reg_no_src1, control_unit_1_reg_no_src2;
  wire [7:0] control_unit_1_imm;
  wire [9:0] control_unit_1_mem_address;
  wire [11:0] control_unit_1_jump_imm, multiplexer_1_out, pc_12_1_pc_value;
  wire [19:0] alu_1_result, multiplexer_2_out, ram_1_data, reg_file_16_1_o1, reg_file_16_1_o2, rom_1_data;

  Clock clock_1 (.out(clock_1_out));
  pc_12 pc_12_1 (
    .mux_enable(1'b1), .select_bits_00f_01a_11l(in_2), .pc_load(in_3), .Clk(clock_1_out), .C_out(out_6),
    .C_in(in_4), .add_value(multiplexer_1_out), .pc_value(pc_12_1_pc_value));
  Multiplexer #(.width(12), .enable("false")) multiplexer_1 (
    .in0({in_5, 1'b1}), .in1(control_unit_1_jump_imm), .out(multiplexer_1_out), .sel(or_1_out));
  ROM #(.addrWidth(12), .dataWidth(20)) rom_1 (.addr(pc_12_1_pc_value), .data(rom_1_data), .sel(1'b1));
  or or_1 (or_1_out, control_unit_1_jump_imm_sel, alu_1_out_9);
  control_unit control_unit_1 (
    .opcode(rom_1_data[19:16]), .inst_left(rom_1_data[15:0]),
    .mem_store_enable(control_unit_1_mem_store_enable), .jump_imm_sel(control_unit_1_jump_imm_sel),
    .jump_imm(control_unit_1_jump_imm), .reg_load_enable(control_unit_1_reg_load_enable),
    .mem_load_enable(control_unit_1_mem_load_enable), .mem_address(control_unit_1_mem_address),
    .reg_no_dest(control_unit_1_reg_no_dest), .reg_no_src1(control_unit_1_reg_no_src1),
    .reg_no_src2(control_unit_1_reg_no_src2), .imm(control_unit_1_imm));
  reg_file_16 reg_file_16_1 (
    .s1_mux_enable(1'b1), .s1_4(control_unit_1_reg_no_src2), .s0_mux_enable(1'b1),
    .s0_4(control_unit_1_reg_no_src1), .enable_decoder_load(control_unit_1_reg_load_enable),
    .input_20bit(multiplexer_2_out), .o1(reg_file_16_1_o1), .o2(reg_file_16_1_o2), .reg_mux_enable(1'b1),
    .clk_fehmi(clock_1_out), .dest(control_unit_1_reg_no_dest));
  alu alu_1 (
    .i0(reg_file_16_1_o1), .i1(reg_file_16_1_o2), .result(alu_1_result), .c_in(in_1),
    .opcode(rom_1_data[19:16]), .enable_result(1'b1), .OF(out_7), .imm(control_unit_1_imm),
    .out_9(alu_1_out_9));
  Multiplexer #(.width(20)) multiplexer_2 (
    .in0(alu_1_result), .in1(ram_1_data), .out(multiplexer_2_out), .sel(control_unit_1_mem_load_enable),
    .en(1'b1));
  RAM #(.addrWidth(10), .dataWidth(20), .bus("separate")) ram_1 (
    .addr(control_unit_1_mem_address), .din(reg_file_16_1_o1), .data(ram_1_data),
    .str(control_unit_1_mem_store_enable), .sel(1'b1), .clk(clock_1_out), .ld(control_unit_1_mem_load_enable));  // open: clr

  // Notes on the sheet:
  //   contents of rom_1 (hex, n*v repeats v):
  //   0 1000 2000 3000 4000 5000 6000 7000 8000 9000 a000 b000 c000 d000 e000 f000 5010d 520f4 43020 f3001
  //   f2002 4001 5002 16450 27450 38450 89400 7a4f0 6b4f0 fa002 fb003 fc004 f9005 2 1003 2004 3005 500fc
  //   50001 910ff 5b333 5c555 1bbc0 fb006 f006 9fb02 5ffff ecfff fc007 ff008 dffdd
  //   OPCODE
endmodule

module control_unit (
  input  [3:0] opcode,
  input  [15:0] inst_left,
  output mem_store_enable,
  output reg_load_enable,
  output mem_load_enable,
  output [9:0] mem_address,
  output [3:0] reg_no_dest,
  output [3:0] reg_no_src1,
  output [3:0] reg_no_src2,
  output [7:0] imm,
  output [11:0] jump_imm,
  output jump_imm_sel
);

  wire decoder_1_out1, decoder_1_out2, decoder_1_out3, decoder_1_out4, decoder_1_out5, decoder_1_out6,
       decoder_1_out7, decoder_1_out8, decoder_1_out9, decoder_1_out10, decoder_1_out11, decoder_1_out12,
       decoder_1_out14, or_1_out, or_2_out, or_3_out;
  wire [11:0] bit_extender_1_out;
  wire [15:0] controlled_buffer_1_out, controlled_buffer_4_out, controlled_buffer_8_out;
  wire [15:8] controlled_buffer_3_out;
  wire [15:10] controlled_buffer_2_out, controlled_buffer_5_out;

  assign controlled_buffer_1_out = or_1_out ? inst_left : 16'bz;  // Controlled_Buffer controlled_buffer_1
  or or_1 (or_1_out, decoder_1_out9, decoder_1_out10, decoder_1_out11, decoder_1_out12, decoder_1_out14);
  assign {controlled_buffer_2_out, mem_address} = mem_load_enable ? inst_left : 16'bz;  // Controlled_Buffer controlled_buffer_2
  assign {controlled_buffer_3_out, imm} = or_3_out ? inst_left : 16'bz;  // Controlled_Buffer controlled_buffer_3
  Decoder #(.select(4), .enable("false")) decoder_1 (
    .out0(mem_load_enable), .out1(decoder_1_out1), .out2(decoder_1_out2), .out3(decoder_1_out3),
    .out4(decoder_1_out4), .out5(decoder_1_out5), .out6(decoder_1_out6), .out7(decoder_1_out7),
    .out8(decoder_1_out8), .out9(decoder_1_out9), .out10(decoder_1_out10), .out11(decoder_1_out11),
    .out12(decoder_1_out12), .out13(jump_imm_sel), .out14(decoder_1_out14), .out15(mem_store_enable),
    .sel(opcode));
  or or_2 (or_2_out, decoder_1_out1, decoder_1_out2, decoder_1_out3, decoder_1_out4);
  assign controlled_buffer_4_out = or_2_out ? inst_left : 16'bz;  // Controlled_Buffer controlled_buffer_4
  assign {controlled_buffer_5_out, mem_address} = mem_store_enable ? inst_left : 16'bz;  // Controlled_Buffer controlled_buffer_5
  assign bit_extender_1_out = {{4{controlled_buffer_1_out[7]}}, controlled_buffer_1_out[7:0]};  // Bit_Extender bit_extender_1
  or or_3 (or_3_out, decoder_1_out5, decoder_1_out6, decoder_1_out7, decoder_1_out8);
  assign reg_no_dest = mem_load_enable ? controlled_buffer_2_out[15:12] : 4'bz;  // Controlled_Buffer controlled_buffer_6
  assign reg_no_dest = or_3_out ? controlled_buffer_3_out[15:12] : 4'bz;  // Controlled_Buffer controlled_buffer_7
  assign controlled_buffer_8_out = jump_imm_sel ? inst_left : 16'bz;  // Controlled_Buffer controlled_buffer_8
  assign jump_imm = or_1_out ? bit_extender_1_out : 12'bz;  // Controlled_Buffer controlled_buffer_9
  assign reg_no_dest = or_2_out ? controlled_buffer_4_out[15:12] : 4'bz;  // Controlled_Buffer controlled_buffer_10
  assign reg_no_src1 = or_3_out ? controlled_buffer_3_out[11:8] : 4'bz;  // Controlled_Buffer controlled_buffer_11
  assign jump_imm = jump_imm_sel ? controlled_buffer_8_out[11:0] : 12'bz;  // Controlled_Buffer controlled_buffer_12
  or or_4 (reg_load_enable, decoder_1_out8, decoder_1_out7, decoder_1_out6, decoder_1_out5, mem_load_enable, decoder_1_out4, decoder_1_out3, decoder_1_out2, decoder_1_out1);
  assign reg_no_src1 = or_2_out ? controlled_buffer_4_out[11:8] : 4'bz;  // Controlled_Buffer controlled_buffer_13
  assign reg_no_src2 = or_2_out ? controlled_buffer_4_out[7:4] : 4'bz;  // Controlled_Buffer controlled_buffer_14
  assign reg_no_src1 = mem_store_enable ? controlled_buffer_5_out[15:12] : 4'bz;  // Controlled_Buffer controlled_buffer_15
  assign reg_no_src1 = or_1_out ? controlled_buffer_1_out[15:12] : 4'bz;  // Controlled_Buffer controlled_buffer_16
  assign reg_no_src2 = or_1_out ? controlled_buffer_1_out[11:8] : 4'bz;  // Controlled_Buffer controlled_buffer_17

  // Notes on the sheet:
  //   REGISTER NO
endmodule

// D_LATCH
module dlatch (
  input  \input ,
  input  clk,
  output pos_o
);

  wire and_1_out, and_2_out, nor_1_out, not_1_out;

  not not_1 (not_1_out, \input );
  and and_1 (and_1_out, \input , clk);
  and and_2 (and_2_out, clk, not_1_out);
  nor nor_1 (nor_1_out, and_1_out, pos_o);
  nor nor_2 (pos_o, nor_1_out, and_2_out);
endmodule

// D_FF
module d_ff (
  input  \input ,
  input  clk,
  output pos_o
);

  wire dlatch_1_pos_o, not_1_out;

  not not_1 (not_1_out, clk);
  dlatch dlatch_1 (.\input (\input ), .clk(not_1_out), .pos_o(dlatch_1_pos_o));
  dlatch dlatch_2 (.\input (dlatch_1_pos_o), .clk(clk), .pos_o(pos_o));
endmodule

// PC_12_BASE
module pc_12_bas (
  input  sel0_1,
  input  sel1_1,
  input  sel2_1,
  input  sel3_1,
  input  sel4_1,
  input  sel5_1,
  input  sel6_1,
  input  sel7_1,
  input  sel8_1,
  input  sel9_1,
  input  sel10_1,
  input  sel11_1,
  input  i_0,
  input  i_1,
  input  i_2,
  input  i_3,
  input  i_4,
  input  i_5,
  input  i_6,
  input  i_7,
  input  i_8,
  input  i_9,
  input  i_10,
  input  i_11,
  input  sel0_0,
  input  sel1_0,
  input  sel2_0,
  input  sel3_0,
  input  sel4_0,
  input  sel5_0,
  input  sel6_0,
  input  sel7_0,
  input  sel8_0,
  input  sel9_0,
  input  sel10_0,
  input  sel11_0,
  input  init_0,
  input  init_1,
  input  init_2,
  input  init_3,
  input  init_4,
  input  init_5,
  input  init_6,
  input  init_7,
  input  init_8,
  input  init_9,
  input  init_10,
  input  init_11,
  input  clk,
  output o_0,
  output o_1,
  output o_2,
  output o_3,
  output o_4,
  output o_5,
  output o_6,
  output o_7,
  output o_8,
  output o_9,
  output o_10,
  output o_11
);

  wire multiplexer_1_out, multiplexer_3_out, multiplexer_4_out, multiplexer_5_out, multiplexer_6_out,
       multiplexer_7_out, multiplexer_8_out, multiplexer_9_out, multiplexer_10_out, multiplexer_11_out,
       multiplexer_12_out;

  Multiplexer multiplexer_1 (.in0(i_0), .in1(init_0), .out(multiplexer_1_out), .sel(sel0_0), .en(sel0_1));
  Multiplexer multiplexer_2 (.in0(i_1), .in1(init_1), .sel(sel1_0), .en(sel1_1));  // open: out
  Multiplexer multiplexer_3 (.in0(i_2), .in1(init_2), .out(multiplexer_3_out), .sel(sel2_0), .en(sel2_1));
  Multiplexer multiplexer_4 (.in0(i_3), .in1(init_3), .out(multiplexer_4_out), .sel(sel3_0), .en(sel3_1));
  Multiplexer multiplexer_5 (.in0(i_4), .in1(init_4), .out(multiplexer_5_out), .sel(sel4_0), .en(sel4_1));
  Multiplexer multiplexer_6 (.in0(i_5), .in1(init_5), .out(multiplexer_6_out), .sel(sel5_0), .en(sel5_1));
  Multiplexer multiplexer_7 (.in0(i_6), .in1(init_6), .out(multiplexer_7_out), .sel(sel6_0), .en(sel6_1));
  Multiplexer multiplexer_8 (.in0(i_7), .in1(init_7), .out(multiplexer_8_out), .sel(sel7_0), .en(sel7_1));
  Multiplexer multiplexer_9 (.in0(i_8), .in1(init_8), .out(multiplexer_9_out), .sel(sel8_0), .en(sel8_1));
  Multiplexer multiplexer_10 (.in0(i_9), .in1(init_9), .out(multiplexer_10_out), .sel(sel9_0), .en(sel9_1));
  Multiplexer multiplexer_11 (.in0(i_10), .in1(init_10), .out(multiplexer_11_out), .sel(sel10_0), .en(sel10_1));
  Multiplexer multiplexer_12 (.in0(i_11), .in1(init_11), .out(multiplexer_12_out), .sel(sel11_0), .en(sel11_1));
  d_ff d_ff_1 (.\input (multiplexer_1_out), .clk(clk), .pos_o(o_0));
  d_ff d_ff_2 (.clk(clk), .pos_o(o_1));  // open: input
  d_ff d_ff_3 (.\input (multiplexer_3_out), .clk(clk), .pos_o(o_2));
  d_ff d_ff_4 (.\input (multiplexer_4_out), .clk(clk), .pos_o(o_3));
  d_ff d_ff_5 (.\input (multiplexer_5_out), .clk(clk), .pos_o(o_4));
  d_ff d_ff_6 (.\input (multiplexer_6_out), .clk(clk), .pos_o(o_5));
  d_ff d_ff_7 (.\input (multiplexer_7_out), .clk(clk), .pos_o(o_6));
  d_ff d_ff_8 (.\input (multiplexer_8_out), .clk(clk), .pos_o(o_7));
  d_ff d_ff_9 (.\input (multiplexer_9_out), .clk(clk), .pos_o(o_8));
  d_ff d_ff_10 (.\input (multiplexer_10_out), .clk(clk), .pos_o(o_9));
  d_ff d_ff_11 (.\input (multiplexer_11_out), .clk(clk), .pos_o(o_10));
  d_ff d_ff_12 (.\input (multiplexer_12_out), .clk(clk), .pos_o(o_11));
endmodule

// PC
module pc_12 (
  input  mux_enable,
  input  C_in,
  input  [1:0] select_bits_00f_01a_11l,
  input  [11:0] pc_load,
  input  Clk,
  input  [11:0] add_value,
  output [11:0] pc_value,
  output C_out
);

  wire [11:0] full_adder_12_1_o_sum_0;

  pc_12_base pc_12_base_1 (
    .init_0(pc_load[0]), .init_1(pc_load[1]), .init_2(pc_load[2]), .init_3(pc_load[3]), .init_4(pc_load[4]),
    .init_5(pc_load[5]), .init_6(pc_load[6]), .init_7(pc_load[7]), .init_8(pc_load[8]), .init_9(pc_load[9]),
    .init_10(pc_load[10]), .init_11(pc_load[11]), .o_0(pc_value[0]), .o_1(pc_value[1]), .o_2(pc_value[2]),
    .o_3(pc_value[3]), .o_4(pc_value[4]), .o_5(pc_value[5]), .o_6(pc_value[6]), .o_7(pc_value[7]),
    .o_8(pc_value[8]), .o_9(pc_value[9]), .o_10(pc_value[10]), .o_11(pc_value[11]),
    .select(select_bits_00f_01a_11l), .enable(mux_enable), .clk(Clk), .feedback(pc_value),
    .feedback_sum(full_adder_12_1_o_sum_0));
  full_adder_12 full_adder_12_1 (
    .i_0_0(pc_value[0]), .i_0_1(pc_value[1]), .i_0_2(pc_value[2]), .i_0_3(pc_value[3]), .i_0_4(pc_value[4]),
    .i_0_5(pc_value[5]), .i_0_6(pc_value[6]), .i_0_7(pc_value[7]), .i_0_8(pc_value[8]), .i_0_9(pc_value[9]),
    .i_0_10(pc_value[10]), .i_0_11(pc_value[11]), .o_sum_0(full_adder_12_1_o_sum_0[0]),
    .o_sum_1(full_adder_12_1_o_sum_0[1]), .o_sum_2(full_adder_12_1_o_sum_0[2]),
    .o_sum_3(full_adder_12_1_o_sum_0[3]), .o_sum_4(full_adder_12_1_o_sum_0[4]),
    .o_sum_5(full_adder_12_1_o_sum_0[5]), .o_sum_6(full_adder_12_1_o_sum_0[6]),
    .o_sum_7(full_adder_12_1_o_sum_0[7]), .o_sum_8(full_adder_12_1_o_sum_0[8]),
    .o_sum_9(full_adder_12_1_o_sum_0[9]), .o_sum_10(full_adder_12_1_o_sum_0[10]),
    .o_sum_11(full_adder_12_1_o_sum_0[11]), .C_in(C_in), .i_1_0(add_value[0]), .i_1_1(add_value[1]),
    .i_1_2(add_value[2]), .i_1_3(add_value[3]), .i_1_4(add_value[4]), .i_1_5(add_value[5]),
    .i_1_6(add_value[6]), .i_1_7(add_value[7]), .i_1_8(add_value[8]), .i_1_9(add_value[9]),
    .i_1_10(add_value[10]), .i_1_11(add_value[11]), .C_out(C_out));
endmodule

// FA_BASE
module full_adder_base (
  input  i_0,
  input  i_1,
  input  C_in,
  output o_sum,
  output c_out
);

  wire and_1_out, and_2_out, xor_1_out;

  xor xor_1 (xor_1_out, i_0, i_1);
  and and_1 (and_1_out, i_0, i_1);
  xor xor_2 (o_sum, xor_1_out, C_in);
  and and_2 (and_2_out, xor_1_out, C_in);
  or or_1 (c_out, and_2_out, and_1_out);
endmodule

// FA_12
module full_adder_12 (
  input  C_in,
  input  i_0_0,
  input  i_0_1,
  input  i_0_2,
  input  i_0_3,
  input  i_0_4,
  input  i_0_5,
  input  i_0_6,
  input  i_0_7,
  input  i_0_8,
  input  i_0_9,
  input  i_0_10,
  input  i_0_11,
  input  i_1_0,
  input  i_1_1,
  input  i_1_2,
  input  i_1_3,
  input  i_1_4,
  input  i_1_5,
  input  i_1_6,
  input  i_1_7,
  input  i_1_8,
  input  i_1_9,
  input  i_1_10,
  input  i_1_11,
  output o_sum_0,
  output o_sum_1,
  output o_sum_2,
  output o_sum_3,
  output o_sum_4,
  output o_sum_5,
  output o_sum_6,
  output o_sum_7,
  output o_sum_8,
  output o_sum_9,
  output o_sum_10,
  output C_out,
  output o_sum_11
);

  wire full_adder_4_1_c_out, full_adder_4_2_c_out;

  full_adder_4 full_adder_4_1 (
    .i_0_0(i_0_0), .i_0_1(i_0_1), .i_0_2(i_0_2), .i_0_3(i_0_3), .o_sum_0(o_sum_0), .o_sum_1(o_sum_1),
    .o_sum_2(o_sum_2), .o_sum_3(o_sum_3), .i_1_0(i_1_0), .i_1_1(i_1_1), .i_1_2(i_1_2), .i_1_3(i_1_3),
    .c_in(C_in), .c_out(full_adder_4_1_c_out));
  full_adder_4 full_adder_4_2 (
    .i_0_0(i_0_4), .i_0_1(i_0_5), .i_0_2(i_0_6), .i_0_3(i_0_7), .o_sum_0(o_sum_4), .o_sum_1(o_sum_5),
    .o_sum_2(o_sum_6), .o_sum_3(o_sum_7), .i_1_0(i_1_4), .i_1_1(i_1_5), .i_1_2(i_1_6), .i_1_3(i_1_7),
    .c_in(full_adder_4_1_c_out), .c_out(full_adder_4_2_c_out));
  full_adder_4 full_adder_4_3 (
    .i_0_0(i_0_8), .i_0_1(i_0_9), .i_0_2(i_0_10), .i_0_3(i_0_11), .o_sum_0(o_sum_8), .o_sum_1(o_sum_9),
    .o_sum_2(o_sum_10), .o_sum_3(o_sum_11), .i_1_0(i_1_8), .i_1_1(i_1_9), .i_1_2(i_1_10), .i_1_3(i_1_11),
    .c_in(full_adder_4_2_c_out), .c_out(C_out));
endmodule

// FA_4
module full_adder_4 (
  input  c_in,
  input  i_0_0,
  input  i_0_1,
  input  i_0_2,
  input  i_0_3,
  input  i_1_0,
  input  i_1_1,
  input  i_1_2,
  input  i_1_3,
  output o_sum_0,
  output o_sum_1,
  output o_sum_2,
  output o_sum_3,
  output c_out
);

  wire full_adder_base_1_c_out, full_adder_base_2_c_out, full_adder_base_3_c_out;

  full_adder_base full_adder_base_1 (
    .i_0(i_0_0), .i_1(i_1_0), .C_in(c_in), .o_sum(o_sum_0), .c_out(full_adder_base_1_c_out));
  full_adder_base full_adder_base_2 (
    .i_0(i_0_1), .i_1(i_1_1), .C_in(full_adder_base_1_c_out), .o_sum(o_sum_1), .c_out(full_adder_base_2_c_out));
  full_adder_base full_adder_base_3 (
    .i_0(i_0_2), .i_1(i_1_2), .C_in(full_adder_base_2_c_out), .o_sum(o_sum_2), .c_out(full_adder_base_3_c_out));
  full_adder_base full_adder_base_4 (
    .i_0(i_0_3), .i_1(i_1_3), .C_in(full_adder_base_3_c_out), .o_sum(o_sum_3), .c_out(c_out));
endmodule

// FA_20
module full_adder_20 (
  input  c_in,
  input  [19:0] i_0,
  input  [19:0] i_1,
  output [19:0] o_0,
  output c_out
);

  wire full_adder_4_1_c_out, full_adder_4_2_c_out, full_adder_4_3_c_out, full_adder_4_4_c_out;

  full_adder_4 full_adder_4_1 (
    .i_0_0(i_0[0]), .i_0_1(i_0[1]), .i_0_2(i_0[2]), .i_0_3(i_0[3]), .o_sum_0(o_0[0]), .o_sum_1(o_0[1]),
    .o_sum_2(o_0[2]), .o_sum_3(o_0[3]), .i_1_0(i_1[0]), .i_1_1(i_1[1]), .i_1_2(i_1[2]), .i_1_3(i_1[3]),
    .c_in(c_in), .c_out(full_adder_4_1_c_out));
  full_adder_4 full_adder_4_2 (
    .i_0_0(i_0[4]), .i_0_1(i_0[5]), .i_0_2(i_0[6]), .i_0_3(i_0[7]), .o_sum_0(o_0[4]), .o_sum_1(o_0[5]),
    .o_sum_2(o_0[6]), .o_sum_3(o_0[7]), .i_1_0(i_1[4]), .i_1_1(i_1[5]), .i_1_2(i_1[6]), .i_1_3(i_1[7]),
    .c_in(full_adder_4_1_c_out), .c_out(full_adder_4_2_c_out));
  full_adder_4 full_adder_4_3 (
    .i_0_0(i_0[8]), .i_0_1(i_0[9]), .i_0_2(i_0[10]), .i_0_3(i_0[11]), .o_sum_0(o_0[8]), .o_sum_1(o_0[9]),
    .o_sum_2(o_0[10]), .o_sum_3(o_0[11]), .i_1_0(i_1[8]), .i_1_1(i_1[9]), .i_1_2(i_1[10]), .i_1_3(i_1[11]),
    .c_in(full_adder_4_2_c_out), .c_out(full_adder_4_3_c_out));
  full_adder_4 full_adder_4_4 (
    .i_0_0(i_0[12]), .i_0_1(i_0[13]), .i_0_2(i_0[14]), .i_0_3(i_0[15]), .o_sum_0(o_0[12]), .o_sum_1(o_0[13]),
    .o_sum_2(o_0[14]), .o_sum_3(o_0[15]), .i_1_0(i_1[12]), .i_1_1(i_1[13]), .i_1_2(i_1[14]), .i_1_3(i_1[15]),
    .c_in(full_adder_4_3_c_out), .c_out(full_adder_4_4_c_out));
  full_adder_4 full_adder_4_5 (
    .i_0_0(i_0[16]), .i_0_1(i_0[17]), .i_0_2(i_0[18]), .i_0_3(i_0[19]), .o_sum_0(o_0[16]), .o_sum_1(o_0[17]),
    .o_sum_2(o_0[18]), .o_sum_3(o_0[19]), .i_1_0(i_1[16]), .i_1_1(i_1[17]), .i_1_2(i_1[18]), .i_1_3(i_1[19]),
    .c_in(full_adder_4_4_c_out), .c_out(c_out));
endmodule

module pc_12_base (
  input  [11:0] feedback,
  input  [11:0] feedback_sum,
  input  [1:0] select,
  input  enable,
  input  init_0,
  input  init_1,
  input  init_2,
  input  init_3,
  input  init_4,
  input  init_5,
  input  init_6,
  input  init_7,
  input  init_8,
  input  init_9,
  input  init_10,
  input  init_11,
  input  clk,
  output o_0,
  output o_1,
  output o_2,
  output o_3,
  output o_4,
  output o_5,
  output o_6,
  output o_7,
  output o_8,
  output o_9,
  output o_10,
  output o_11
);

  wire multiplexer_1_out, multiplexer_2_out, multiplexer_3_out, multiplexer_4_out, multiplexer_5_out,
       multiplexer_6_out, multiplexer_7_out, multiplexer_8_out, multiplexer_9_out, multiplexer_10_out,
       multiplexer_11_out, multiplexer_12_out;

  Multiplexer #(.select(2)) multiplexer_1 (
    .in0(feedback[0]), .in1(feedback_sum[0]), .in3(init_0), .out(multiplexer_1_out), .sel(select), .en(enable));  // open: in2
  Multiplexer #(.select(2)) multiplexer_2 (
    .in0(feedback[1]), .in1(feedback_sum[1]), .in3(init_1), .out(multiplexer_2_out), .sel(select), .en(enable));  // open: in2
  Multiplexer #(.select(2)) multiplexer_3 (
    .in0(feedback[2]), .in1(feedback_sum[2]), .in3(init_2), .out(multiplexer_3_out), .sel(select), .en(enable));  // open: in2
  Multiplexer #(.select(2)) multiplexer_4 (
    .in0(feedback[3]), .in1(feedback_sum[3]), .in3(init_3), .out(multiplexer_4_out), .sel(select), .en(enable));  // open: in2
  Multiplexer #(.select(2)) multiplexer_5 (
    .in0(feedback[4]), .in1(feedback_sum[4]), .in3(init_4), .out(multiplexer_5_out), .sel(select), .en(enable));  // open: in2
  Multiplexer #(.select(2)) multiplexer_6 (
    .in0(feedback[5]), .in1(feedback_sum[5]), .in3(init_5), .out(multiplexer_6_out), .sel(select), .en(enable));  // open: in2
  Multiplexer #(.select(2)) multiplexer_7 (
    .in0(feedback[6]), .in1(feedback_sum[6]), .in3(init_6), .out(multiplexer_7_out), .sel(select), .en(enable));  // open: in2
  Multiplexer #(.select(2)) multiplexer_8 (
    .in0(feedback[7]), .in1(feedback_sum[7]), .in3(init_7), .out(multiplexer_8_out), .sel(select), .en(enable));  // open: in2
  Multiplexer #(.select(2)) multiplexer_9 (
    .in0(feedback[8]), .in1(feedback_sum[8]), .in3(init_8), .out(multiplexer_9_out), .sel(select), .en(enable));  // open: in2
  Multiplexer #(.select(2)) multiplexer_10 (
    .in0(feedback[9]), .in1(feedback_sum[9]), .in3(init_9), .out(multiplexer_10_out), .sel(select),
    .en(enable));  // open: in2
  Multiplexer #(.select(2)) multiplexer_11 (
    .in0(feedback[10]), .in1(feedback_sum[10]), .in3(init_10), .out(multiplexer_11_out), .sel(select),
    .en(enable));  // open: in2
  Multiplexer #(.select(2)) multiplexer_12 (
    .in0(feedback[11]), .in1(feedback_sum[11]), .in3(init_11), .out(multiplexer_12_out), .sel(select),
    .en(enable));  // open: in2
  d_ff d_ff_1 (.\input (multiplexer_1_out), .clk(clk), .pos_o(o_0));
  d_ff d_ff_2 (.\input (multiplexer_2_out), .clk(clk), .pos_o(o_1));
  d_ff d_ff_3 (.\input (multiplexer_3_out), .clk(clk), .pos_o(o_2));
  d_ff d_ff_4 (.\input (multiplexer_4_out), .clk(clk), .pos_o(o_3));
  d_ff d_ff_5 (.\input (multiplexer_5_out), .clk(clk), .pos_o(o_4));
  d_ff d_ff_6 (.\input (multiplexer_6_out), .clk(clk), .pos_o(o_5));
  d_ff d_ff_7 (.\input (multiplexer_7_out), .clk(clk), .pos_o(o_6));
  d_ff d_ff_8 (.\input (multiplexer_8_out), .clk(clk), .pos_o(o_7));
  d_ff d_ff_9 (.\input (multiplexer_9_out), .clk(clk), .pos_o(o_8));
  d_ff d_ff_10 (.\input (multiplexer_10_out), .clk(clk), .pos_o(o_9));
  d_ff d_ff_11 (.\input (multiplexer_11_out), .clk(clk), .pos_o(o_10));
  d_ff d_ff_12 (.\input (multiplexer_12_out), .clk(clk), .pos_o(o_11));
endmodule

// ALU
module alu (
  input  [3:0] opcode,
  input  enable_result,
  input  c_in,
  input  [19:0] i0,
  input  [19:0] i1,
  input  [7:0] imm,
  output OF,
  output [19:0] result,
  output out_9
);

  wire decoder_1_out5, decoder_1_out6, decoder_1_out7, decoder_1_out8, decoder_1_out9, decoder_1_out10,
       decoder_1_out11, decoder_1_out12, decoder_1_out14, full_adder_20_1_c_out, or_1_out, or_3_out;
  wire [19:0] and_1_out, bit_extender_1_out, full_adder_20_1_o_0, multiplexer_1_out, multiplexer_3_out,
       not_1_out, or_2_out, xor_1_out;
  wire [20:0] multiplexer_2_out;
  wire [20:1] adder_1_out;

  assign bit_extender_1_out = {{12{imm[7]}}, imm};  // Bit_Extender bit_extender_1
  assign not_1_out = ~i1;  // NOT_Gate not_1, 20 bits wide
  Multiplexer #(.width(20), .enable("false")) multiplexer_1 (
    .in0(i1), .in1(bit_extender_1_out), .out(multiplexer_1_out), .sel(or_3_out));
  full_adder_20 full_adder_20_1 (
    .i_0(not_1_out), .o_0(full_adder_20_1_o_0), .c_in(1'b0), .i_1(20'h1), .c_out(full_adder_20_1_c_out));
  Multiplexer #(.select(4), .width(21), .enable("false")) multiplexer_2 (
    .in0({21{1'b0}}), .in1({21{1'b0}}), .in2({21{1'b0}}), .in3({21{1'b0}}), .in4({21{1'b0}}),
    .in5({21{1'b0}}), .in6({21{1'b0}}), .in7({21{1'b0}}), .in8({21{1'b0}}), .in9({adder_1_out, opcode[3]}),
    .in10({adder_1_out, opcode[3]}), .in11({adder_1_out, opcode[3]}), .in12({adder_1_out, opcode[3]}),
    .in13({21{1'b0}}), .in14({adder_1_out, opcode[3]}), .in15({21{1'b0}}), .out(multiplexer_2_out),
    .sel(opcode));
  Multiplexer #(.width(20), .enable("false")) multiplexer_3 (
    .in0(multiplexer_1_out), .in1(full_adder_20_1_o_0), .out(multiplexer_3_out), .sel(or_1_out));
  or or_1 (or_1_out, decoder_1_out9, decoder_1_out10, decoder_1_out11, decoder_1_out12, decoder_1_out14);
  branch_comparator branch_comparator_1 (
    .opcode({multiplexer_2_out[0], opcode[2:0]}), .sub_result(multiplexer_2_out[20:1]), .jump_select(out_9));
  Adder #(.width(20)) adder_1 (.a(i0), .b(multiplexer_3_out), .out(adder_1_out), .cin(c_in), .cout(OF));
  assign and_1_out = i0 & multiplexer_1_out;  // AND_Gate and_1, 20 bits wide
  assign xor_1_out = i0 ^ multiplexer_1_out;  // XOR_Gate xor_1, 20 bits wide
  assign or_2_out = i0 | multiplexer_1_out;  // OR_Gate or_2, 20 bits wide
  or or_3 (or_3_out, decoder_1_out5, decoder_1_out6, decoder_1_out7, decoder_1_out8);
  Multiplexer #(.select(4), .width(20)) multiplexer_4 (
    .in1(xor_1_out), .in2(or_2_out), .in3(and_1_out), .in4(adder_1_out), .in5(adder_1_out), .in6(or_2_out),
    .in7(xor_1_out), .in8(and_1_out), .out(result), .sel(opcode), .en(enable_result));  // open: in0, in9, in10, in11, in12, in13, in14, in15
  Decoder #(.select(4), .enable("false")) decoder_1 (
    .out5(decoder_1_out5), .out6(decoder_1_out6), .out7(decoder_1_out7), .out8(decoder_1_out8),
    .out9(decoder_1_out9), .out10(decoder_1_out10), .out11(decoder_1_out11), .out12(decoder_1_out12),
    .out14(decoder_1_out14), .sel(opcode));  // open: out0, out1, out2, out3, out4, out13, out15
endmodule

module reg_1bit_pl (
  input  enable,
  input  sel_0f_1l,
  input  \input ,
  input  clk,
  output \output 
);

  wire multiplexer_1_out;

  Multiplexer multiplexer_1 (.in0(\output ), .in1(\input ), .out(multiplexer_1_out), .sel(sel_0f_1l), .en(enable));
  d_ff d_ff_1 (.\input (multiplexer_1_out), .clk(clk), .pos_o(\output ));
endmodule

module reg_4bit_pl (
  input  enable,
  input  sel_0f_1l,
  input  [3:0] _4bit_in,
  input  clk,
  output [3:0] _4bit_out
);

  reg_1bit_pl reg_1bit_pl_1 (
    .\input (_4bit_in[0]), .\output (_4bit_out[0]), .sel_0f_1l(sel_0f_1l), .enable(enable), .clk(clk));
  reg_1bit_pl reg_1bit_pl_2 (
    .\input (_4bit_in[1]), .\output (_4bit_out[1]), .sel_0f_1l(sel_0f_1l), .enable(enable), .clk(clk));
  reg_1bit_pl reg_1bit_pl_3 (
    .\input (_4bit_in[2]), .\output (_4bit_out[2]), .sel_0f_1l(sel_0f_1l), .enable(enable), .clk(clk));
  reg_1bit_pl reg_1bit_pl_4 (
    .\input (_4bit_in[3]), .\output (_4bit_out[3]), .sel_0f_1l(sel_0f_1l), .enable(enable), .clk(clk));
endmodule

// reg_20
module reg_20bit_pl (
  input  enable,
  input  sel_0f_1l,
  input  [19:0] in_3,
  input  clk,
  output [19:0] out_5
);

  reg_4bit_pl reg_4bit_pl_1 (
    ._4bit_in(in_3[3:0]), ._4bit_out(out_5[3:0]), .sel_0f_1l(sel_0f_1l), .enable(enable), .clk(clk));
  reg_4bit_pl reg_4bit_pl_2 (
    ._4bit_in(in_3[7:4]), ._4bit_out(out_5[7:4]), .sel_0f_1l(sel_0f_1l), .enable(enable), .clk(clk));
  reg_4bit_pl reg_4bit_pl_3 (
    ._4bit_in(in_3[11:8]), ._4bit_out(out_5[11:8]), .sel_0f_1l(sel_0f_1l), .enable(enable), .clk(clk));
  reg_4bit_pl reg_4bit_pl_4 (
    ._4bit_in(in_3[15:12]), ._4bit_out(out_5[15:12]), .sel_0f_1l(sel_0f_1l), .enable(enable), .clk(clk));
  reg_4bit_pl reg_4bit_pl_5 (
    ._4bit_in(in_3[19:16]), ._4bit_out(out_5[19:16]), .sel_0f_1l(sel_0f_1l), .enable(enable), .clk(clk));
endmodule

module reg_file_16 (
  input  s1_mux_enable,
  input  [3:0] s1_4,
  input  s0_mux_enable,
  input  [3:0] s0_4,
  input  [3:0] dest,
  input  enable_decoder_load,
  input  reg_mux_enable,
  input  [19:0] input_20bit,
  input  clk_fehmi,
  output [19:0] o1,
  output [19:0] o2
);

  wire decoder_1_out0, decoder_1_out1, decoder_1_out2, decoder_1_out3, decoder_1_out4, decoder_1_out5,
       decoder_1_out6, decoder_1_out7, decoder_1_out8, decoder_1_out9, decoder_1_out10, decoder_1_out11,
       decoder_1_out12, decoder_1_out13, decoder_1_out14, decoder_1_out15;
  wire [19:0] reg_20bit_pl_1_out_5, reg_20bit_pl_2_out_5, reg_20bit_pl_3_out_5, reg_20bit_pl_4_out_5,
       reg_20bit_pl_5_out_5, reg_20bit_pl_6_out_5, reg_20bit_pl_7_out_5, reg_20bit_pl_8_out_5,
       reg_20bit_pl_9_out_5, reg_20bit_pl_10_out_5, reg_20bit_pl_11_out_5, reg_20bit_pl_12_out_5,
       reg_20bit_pl_13_out_5, reg_20bit_pl_14_out_5, reg_20bit_pl_15_out_5, reg_20bit_pl_16_out_5;

  Decoder #(.select(4)) decoder_1 (
    .out0(decoder_1_out0), .out1(decoder_1_out1), .out2(decoder_1_out2), .out3(decoder_1_out3),
    .out4(decoder_1_out4), .out5(decoder_1_out5), .out6(decoder_1_out6), .out7(decoder_1_out7),
    .out8(decoder_1_out8), .out9(decoder_1_out9), .out10(decoder_1_out10), .out11(decoder_1_out11),
    .out12(decoder_1_out12), .out13(decoder_1_out13), .out14(decoder_1_out14), .out15(decoder_1_out15),
    .sel(dest), .en(enable_decoder_load));
  reg_20bit_pl reg_20bit_pl_1 (
    .in_3(input_20bit), .out_5(reg_20bit_pl_1_out_5), .sel_0f_1l(decoder_1_out0), .enable(reg_mux_enable),
    .clk(clk_fehmi));
  reg_20bit_pl reg_20bit_pl_2 (
    .in_3(input_20bit), .out_5(reg_20bit_pl_2_out_5), .sel_0f_1l(decoder_1_out1), .enable(reg_mux_enable),
    .clk(clk_fehmi));
  reg_20bit_pl reg_20bit_pl_3 (
    .in_3(input_20bit), .out_5(reg_20bit_pl_3_out_5), .sel_0f_1l(decoder_1_out2), .enable(reg_mux_enable),
    .clk(clk_fehmi));
  reg_20bit_pl reg_20bit_pl_4 (
    .in_3(input_20bit), .out_5(reg_20bit_pl_4_out_5), .sel_0f_1l(decoder_1_out3), .enable(reg_mux_enable),
    .clk(clk_fehmi));
  reg_20bit_pl reg_20bit_pl_5 (
    .in_3(input_20bit), .out_5(reg_20bit_pl_5_out_5), .sel_0f_1l(decoder_1_out4), .enable(reg_mux_enable),
    .clk(clk_fehmi));
  reg_20bit_pl reg_20bit_pl_6 (
    .in_3(input_20bit), .out_5(reg_20bit_pl_6_out_5), .sel_0f_1l(decoder_1_out5), .enable(reg_mux_enable),
    .clk(clk_fehmi));
  reg_20bit_pl reg_20bit_pl_7 (
    .in_3(input_20bit), .out_5(reg_20bit_pl_7_out_5), .sel_0f_1l(decoder_1_out6), .enable(reg_mux_enable),
    .clk(clk_fehmi));
  reg_20bit_pl reg_20bit_pl_8 (
    .in_3(input_20bit), .out_5(reg_20bit_pl_8_out_5), .sel_0f_1l(decoder_1_out7), .enable(reg_mux_enable),
    .clk(clk_fehmi));
  reg_20bit_pl reg_20bit_pl_9 (
    .in_3(input_20bit), .out_5(reg_20bit_pl_9_out_5), .sel_0f_1l(decoder_1_out8), .enable(reg_mux_enable),
    .clk(clk_fehmi));
  reg_20bit_pl reg_20bit_pl_10 (
    .in_3(input_20bit), .out_5(reg_20bit_pl_10_out_5), .sel_0f_1l(decoder_1_out9), .enable(reg_mux_enable),
    .clk(clk_fehmi));
  reg_20bit_pl reg_20bit_pl_11 (
    .in_3(input_20bit), .out_5(reg_20bit_pl_11_out_5), .sel_0f_1l(decoder_1_out10), .enable(reg_mux_enable),
    .clk(clk_fehmi));
  reg_20bit_pl reg_20bit_pl_12 (
    .in_3(input_20bit), .out_5(reg_20bit_pl_12_out_5), .sel_0f_1l(decoder_1_out11), .enable(reg_mux_enable),
    .clk(clk_fehmi));
  reg_20bit_pl reg_20bit_pl_13 (
    .in_3(input_20bit), .out_5(reg_20bit_pl_13_out_5), .sel_0f_1l(decoder_1_out12), .enable(reg_mux_enable),
    .clk(clk_fehmi));
  reg_20bit_pl reg_20bit_pl_14 (
    .in_3(input_20bit), .out_5(reg_20bit_pl_14_out_5), .sel_0f_1l(decoder_1_out13), .enable(reg_mux_enable),
    .clk(clk_fehmi));
  reg_20bit_pl reg_20bit_pl_15 (
    .in_3(input_20bit), .out_5(reg_20bit_pl_15_out_5), .sel_0f_1l(decoder_1_out14), .enable(reg_mux_enable),
    .clk(clk_fehmi));
  reg_20bit_pl reg_20bit_pl_16 (
    .in_3(input_20bit), .out_5(reg_20bit_pl_16_out_5), .sel_0f_1l(decoder_1_out15), .enable(reg_mux_enable),
    .clk(clk_fehmi));
  Multiplexer #(.select(4), .width(20)) multiplexer_1 (
    .in0(reg_20bit_pl_1_out_5), .in1(reg_20bit_pl_2_out_5), .in2(reg_20bit_pl_3_out_5),
    .in3(reg_20bit_pl_4_out_5), .in4(reg_20bit_pl_5_out_5), .in5(reg_20bit_pl_6_out_5),
    .in6(reg_20bit_pl_7_out_5), .in7(reg_20bit_pl_8_out_5), .in8(reg_20bit_pl_9_out_5),
    .in9(reg_20bit_pl_10_out_5), .in10(reg_20bit_pl_11_out_5), .in11(reg_20bit_pl_12_out_5),
    .in12(reg_20bit_pl_13_out_5), .in13(reg_20bit_pl_14_out_5), .in14(reg_20bit_pl_15_out_5),
    .in15(reg_20bit_pl_16_out_5), .out(o1), .sel(s0_4), .en(s0_mux_enable));
  Multiplexer #(.select(4), .width(20)) multiplexer_2 (
    .in0(reg_20bit_pl_1_out_5), .in1(reg_20bit_pl_2_out_5), .in2(reg_20bit_pl_3_out_5),
    .in3(reg_20bit_pl_4_out_5), .in4(reg_20bit_pl_5_out_5), .in5(reg_20bit_pl_6_out_5),
    .in6(reg_20bit_pl_7_out_5), .in7(reg_20bit_pl_8_out_5), .in8(reg_20bit_pl_9_out_5),
    .in9(reg_20bit_pl_10_out_5), .in10(reg_20bit_pl_11_out_5), .in11(reg_20bit_pl_12_out_5),
    .in12(reg_20bit_pl_13_out_5), .in13(reg_20bit_pl_14_out_5), .in14(reg_20bit_pl_15_out_5),
    .in15(reg_20bit_pl_16_out_5), .out(o2), .sel(s1_4), .en(s1_mux_enable));
endmodule

module dinazor (
  input  in_1,
  input  in_2,
  input  [1:0] in_3,
  input  [11:0] in_4,
  input  in_5,
  input  [10:0] in_6,
  output out_7,
  output out_8
);

  wire clock_1_out, control_unit_1_jump_imm_sel, control_unit_1_mem_load_enable,
       control_unit_1_mem_store_enable, control_unit_1_reg_load_enable;
  wire [3:0] control_unit_1_reg_no_dest, control_unit_1_reg_no_src1, control_unit_1_reg_no_src2;
  wire [7:0] control_unit_1_imm;
  wire [9:0] control_unit_1_mem_address;
  wire [11:0] control_unit_1_jump_imm, multiplexer_1_out, pc_12_1_pc_value;
  wire [19:0] alu_1_result, multiplexer_2_out, ram_1_data, reg_file_16_1_o1, reg_file_16_1_o2, rom_1_data;

  Clock clock_1 (.out(clock_1_out));
  pc_12 pc_12_1 (
    .mux_enable(in_1), .select_bits_00f_01a_11l(in_3), .pc_load(in_4), .Clk(clock_1_out), .C_out(out_7),
    .C_in(in_5), .add_value(multiplexer_1_out), .pc_value(pc_12_1_pc_value));
  Multiplexer #(.width(12), .enable("false")) multiplexer_1 (
    .in0({in_6, in_1}), .in1(control_unit_1_jump_imm), .out(multiplexer_1_out),
    .sel(control_unit_1_jump_imm_sel));
  ROM #(.addrWidth(12), .dataWidth(20)) rom_1 (.addr(pc_12_1_pc_value), .data(rom_1_data), .sel(in_1));
  control_unit control_unit_1 (
    .opcode(rom_1_data[19:16]), .inst_left(rom_1_data[15:0]),
    .mem_store_enable(control_unit_1_mem_store_enable), .jump_imm_sel(control_unit_1_jump_imm_sel),
    .jump_imm(control_unit_1_jump_imm), .reg_load_enable(control_unit_1_reg_load_enable),
    .mem_load_enable(control_unit_1_mem_load_enable), .mem_address(control_unit_1_mem_address),
    .reg_no_dest(control_unit_1_reg_no_dest), .reg_no_src1(control_unit_1_reg_no_src1),
    .reg_no_src2(control_unit_1_reg_no_src2), .imm(control_unit_1_imm));
  reg_file_16 reg_file_16_1 (
    .s1_mux_enable(in_1), .s1_4(control_unit_1_reg_no_src2), .s0_mux_enable(in_1),
    .s0_4(control_unit_1_reg_no_src1), .enable_decoder_load(control_unit_1_reg_load_enable),
    .input_20bit(multiplexer_2_out), .o1(reg_file_16_1_o1), .o2(reg_file_16_1_o2), .reg_mux_enable(in_1),
    .clk_fehmi(clock_1_out), .dest(control_unit_1_reg_no_dest));
  alu alu_1 (
    .i0(reg_file_16_1_o1), .i1(reg_file_16_1_o2), .result(alu_1_result), .c_in(in_2),
    .opcode(rom_1_data[19:16]), .enable_result(in_1), .OF(out_8), .imm(control_unit_1_imm));  // open: out_9
  Multiplexer #(.width(20)) multiplexer_2 (
    .in0(alu_1_result), .in1(ram_1_data), .out(multiplexer_2_out), .sel(control_unit_1_mem_load_enable),
    .en(in_1));
  RAM #(.addrWidth(10), .dataWidth(20), .bus("separate")) ram_1 (
    .addr(control_unit_1_mem_address), .din(reg_file_16_1_o1), .data(ram_1_data),
    .str(control_unit_1_mem_store_enable), .sel(in_1), .clk(clock_1_out), .ld(control_unit_1_mem_load_enable));  // open: clr

  // Notes on the sheet:
  //   contents of rom_1 (hex, n*v repeats v):
  //   0 f0001 f0001 6465 78987 ad 8*0 aad 0 0 0 d adad 0 da ad ad 0 0 ad da ada dada 21*0 ad 0 ad
  //   OPCODE
endmodule

module branch_comparator (
  input  [3:0] opcode,
  input  [19:0] sub_result,
  output jump_select
);

  wire and_1_out, and_2_out, and_3_out, and_4_out, nor_1_out, not_1_out, or_1_out, or_2_out;

  not not_1 (not_1_out, sub_result[19]);
  or or_1 (or_1_out, sub_result[18], sub_result[17], sub_result[16], sub_result[15], sub_result[14], sub_result[13], sub_result[12], sub_result[11], sub_result[10], sub_result[9], sub_result[8], sub_result[7], sub_result[6], sub_result[5], sub_result[4], sub_result[3], sub_result[2], sub_result[1], sub_result[0]);
  and and_1 (and_1_out, opcode[2], sub_result[19]);
  and and_2 (and_2_out, not_1_out, or_1_out);
  nor nor_1 (nor_1_out, sub_result[19], sub_result[18], sub_result[17], sub_result[16], sub_result[15], sub_result[14], sub_result[13], sub_result[12], sub_result[11], sub_result[10], sub_result[9], sub_result[8], sub_result[7], sub_result[6], sub_result[5], sub_result[4], sub_result[3], sub_result[2], sub_result[1], sub_result[0]);
  and and_3 (and_3_out, opcode[1], nor_1_out);
  and and_4 (and_4_out, opcode[0], and_2_out);
  or or_2 (or_2_out, and_1_out, and_3_out, and_4_out);
  and and_5 (jump_select, or_2_out, opcode[3]);

  // Notes on the sheet:
  //   n
  //   z
  //   p
endmodule
