// Logisim project deneme1.circ as structural Verilog: 18 circuits, main circuit Datapath
module DFlipFlop (
  input  in_1,
  input  in_2,
  output out_3
);

  wire dlatchh_1_out_2, not_1_out;

  not not_1 (not_1_out, in_2);
  Dlatchh dlatchh_1 (.in_1(in_1), .out_2(dlatchh_1_out_2));
  Dlatchh dlatchh_2 (.in_1(dlatchh_1_out_2), .out_2(out_3));

  // Notes on the sheet:
  //   D Flip Flop
endmodule

module Dlatchh (
  input  in_1,
  output out_2
);

  wire and_1_out, and_2_out, clock_1_out, nor_1_out, not_1_out;

  Clock clock_1 (.out(clock_1_out));
  not not_1 (not_1_out, in_1);
  and and_1 (and_1_out, in_1, clock_1_out);
  and and_2 (and_2_out, clock_1_out, not_1_out);
  nor nor_1 (nor_1_out, and_1_out, out_2);
  nor nor_2 (out_2, nor_1_out, and_2_out);

  // Notes on the sheet:
  //   D latch
endmodule

module registerWithShf (
  input  \İ5 ,
  input  \İ4 ,
  input  \İ3 ,
  input  \İ2 ,
  input  \İ1 ,
  input  \İ0 ,
  input  Shr_in,
  input  \İ7 ,
  input  \İ6 ,
  input  \İ8 ,
  input  Shl_in,
  input  \İ19 ,
  input  \İ18 ,
  input  \İ17 ,
  input  \İ16 ,
  input  \İ15 ,
  input  \İ14 ,
  input  \İ13 ,
  input  \İ12 ,
  input  \İ11 ,
  input  \İ10 ,
  input  \İ9 ,
  input  [1:0] S1S0,
  input  clk,
  output Out_13,
  output Out_19,
  output Out_18,
  output Out_17,
  output Out_16,
  output Out_15,
  output Out_14,
  output Out_12,
  output Out_11,
  output Out_10,
  output Out_9,
  output Out_8,
  output Out_7,
  output Out_6,
  output Out_5,
  output Out_4,
  output Out_3,
  output Out_2,
  output Out_1,
  output Out_0
);

  wire multiplexer_1_out, multiplexer_2_out, multiplexer_3_out, multiplexer_4_out, multiplexer_5_out,
       multiplexer_6_out, multiplexer_7_out, multiplexer_8_out, multiplexer_9_out, multiplexer_10_out,
       multiplexer_11_out, multiplexer_12_out, multiplexer_13_out, multiplexer_14_out, multiplexer_15_out,
       multiplexer_16_out, multiplexer_17_out, multiplexer_18_out, multiplexer_19_out, multiplexer_20_out;

  Multiplexer #(.select(2), .enable("false")) multiplexer_1 (
    .in0(Shr_in), .in1(\İ19 ), .in2(Out_19), .in3(Out_18), .out(multiplexer_1_out), .sel(S1S0));
  DFlipFlop dflipflop_1 (.in_1(multiplexer_1_out), .in_2(clk), .out_3(Out_19));
  Multiplexer #(.select(2), .enable("false")) multiplexer_2 (
    .in0(Out_19), .in1(\İ18 ), .in2(Out_18), .in3(Out_16), .out(multiplexer_2_out), .sel(S1S0));
  DFlipFlop dflipflop_2 (.in_1(multiplexer_2_out), .in_2(clk), .out_3(Out_18));
  Multiplexer #(.select(2), .enable("false")) multiplexer_3 (
    .in0(Out_18), .in1(\İ17 ), .in2(Out_16), .in3(Out_16), .out(multiplexer_3_out), .sel(S1S0));
  Multiplexer #(.select(2), .enable("false")) multiplexer_4 (
    .in0(Out_16), .in1(\İ16 ), .in2(Out_16), .in3(Out_15), .out(multiplexer_4_out), .sel(S1S0));
  DFlipFlop dflipflop_3 (.in_1(multiplexer_3_out), .in_2(clk), .out_3(Out_16));
  DFlipFlop dflipflop_4 (.in_1(multiplexer_4_out), .in_2(clk), .out_3(Out_16));
  Multiplexer #(.select(2), .enable("false")) multiplexer_5 (
    .in0(Out_16), .in1(\İ15 ), .in2(Out_15), .in3(Out_14), .out(multiplexer_5_out), .sel(S1S0));
  DFlipFlop dflipflop_5 (.in_1(multiplexer_5_out), .in_2(clk), .out_3(Out_15));
  Multiplexer #(.select(2), .enable("false")) multiplexer_6 (
    .in0(Out_15), .in1(\İ14 ), .in2(Out_14), .in3(Out_13), .out(multiplexer_6_out), .sel(S1S0));
  Multiplexer #(.select(2), .enable("false")) multiplexer_7 (
    .in0(Out_14), .in1(\İ13 ), .in2(Out_13), .in3(Out_12), .out(multiplexer_7_out), .sel(S1S0));
  DFlipFlop dflipflop_6 (.in_1(multiplexer_6_out), .in_2(clk), .out_3(Out_14));
  DFlipFlop dflipflop_7 (.in_1(multiplexer_7_out), .in_2(clk), .out_3(Out_13));
  Multiplexer #(.select(2), .enable("false")) multiplexer_8 (
    .in0(Out_13), .in1(\İ12 ), .in2(Out_12), .in3(Out_11), .out(multiplexer_8_out), .sel(S1S0));
  DFlipFlop dflipflop_8 (.in_1(multiplexer_8_out), .in_2(clk), .out_3(Out_12));
  Multiplexer #(.select(2), .enable("false")) multiplexer_9 (
    .in0(Out_12), .in1(\İ11 ), .in2(Out_11), .in3(Out_10), .out(multiplexer_9_out), .sel(S1S0));
  DFlipFlop dflipflop_9 (.in_1(multiplexer_9_out), .in_2(clk), .out_3(Out_11));
  Multiplexer #(.select(2), .enable("false")) multiplexer_10 (
    .in0(Out_11), .in1(\İ10 ), .in2(Out_10), .in3(Out_9), .out(multiplexer_10_out), .sel(S1S0));
  DFlipFlop dflipflop_10 (.in_1(multiplexer_10_out), .in_2(clk), .out_3(Out_10));
  Multiplexer #(.select(2), .enable("false")) multiplexer_11 (
    .in0(Out_10), .in1(\İ9 ), .in2(Out_9), .in3(Out_8), .out(multiplexer_11_out), .sel(S1S0));
  Multiplexer #(.select(2), .enable("false")) multiplexer_12 (
    .in0(Out_9), .in1(\İ8 ), .in2(Out_8), .in3(Out_7), .out(multiplexer_12_out), .sel(S1S0));
  DFlipFlop dflipflop_11 (.in_1(multiplexer_11_out), .in_2(clk), .out_3(Out_9));
  DFlipFlop dflipflop_12 (.in_1(multiplexer_12_out), .in_2(clk), .out_3(Out_8));
  Multiplexer #(.select(2), .enable("false")) multiplexer_13 (
    .in0(Out_8), .in1(\İ7 ), .in2(Out_7), .in3(Out_6), .out(multiplexer_13_out), .sel(S1S0));
  DFlipFlop dflipflop_13 (.in_1(multiplexer_13_out), .in_2(clk), .out_3(Out_7));
  Multiplexer #(.select(2), .enable("false")) multiplexer_14 (
    .in0(Out_7), .in1(\İ6 ), .in2(Out_6), .in3(Out_5), .out(multiplexer_14_out), .sel(S1S0));
  DFlipFlop dflipflop_14 (.in_1(multiplexer_14_out), .in_2(clk), .out_3(Out_6));
  Multiplexer #(.select(2), .enable("false")) multiplexer_15 (
    .in0(Out_6), .in1(\İ5 ), .in2(Out_5), .in3(Out_4), .out(multiplexer_15_out), .sel(S1S0));
  DFlipFlop dflipflop_15 (.in_1(multiplexer_15_out), .in_2(clk), .out_3(Out_5));
  Multiplexer #(.select(2), .enable("false")) multiplexer_16 (
    .in0(Out_5), .in1(\İ4 ), .in2(Out_4), .in3(Out_3), .out(multiplexer_16_out), .sel(S1S0));
  DFlipFlop dflipflop_16 (.in_1(multiplexer_16_out), .in_2(clk), .out_3(Out_4));
  Multiplexer #(.select(2), .enable("false")) multiplexer_17 (
    .in0(Out_4), .in1(\İ3 ), .in2(Out_3), .in3(Out_2), .out(multiplexer_17_out), .sel(S1S0));
  DFlipFlop dflipflop_17 (.in_1(multiplexer_17_out), .in_2(clk), .out_3(Out_3));
  Multiplexer #(.select(2), .enable("false")) multiplexer_18 (
    .in0(Out_3), .in1(\İ2 ), .in2(Out_2), .in3(\İ1 ), .out(multiplexer_18_out), .sel(S1S0));
  DFlipFlop dflipflop_18 (.in_1(multiplexer_18_out), .in_2(clk), .out_3(Out_2));
  Multiplexer #(.select(2), .enable("false")) multiplexer_19 (
    .in0(Out_2), .in1(\İ1 ), .in2(\İ1 ), .in3(Out_0), .out(multiplexer_19_out), .sel(S1S0));
  Multiplexer #(.select(2), .enable("false")) multiplexer_20 (
    .in0(\İ1 ), .in1(\İ0 ), .in2(Out_0), .in3(Shl_in), .out(multiplexer_20_out), .sel(S1S0));
  DFlipFlop dflipflop_19 (.in_1(multiplexer_19_out), .in_2(clk), .out_3(\İ1 ));
  DFlipFlop dflipflop_20 (.in_1(multiplexer_20_out), .in_2(clk), .out_3(Out_0));

  assign Out_1 = \İ1 ;
  assign Out_17 = Out_16;

  // Notes on the sheet:
  //   S1S0  FUNC
  //   SHright
  //   00
  //   load
  //   01
  //   10
  //   shleft
  //   11
  //   no change
endmodule

module RegFile (
  input  [19:0] data_in,
  input  WE,
  input  [3:0] adress_of_reg1,
  input  [3:0] which_reg,
  input  [3:0] address_of_reg2,
  input  clk,
  output [19:0] ReadSrc1,
  output [19:0] ReadSrc2
);

  wire and_1_out, and_2_out, and_3_out, and_4_out, and_5_out, and_6_out, and_7_out, and_8_out, and_9_out,
       and_10_out, and_11_out, and_12_out, and_13_out, and_14_out, and_15_out, and_16_out, decoder_1_out0,
       decoder_1_out1, decoder_1_out2, decoder_1_out3, decoder_1_out4, decoder_1_out5, decoder_1_out6,
       decoder_1_out7, decoder_1_out8, decoder_1_out9, decoder_1_out10, decoder_1_out11, decoder_1_out12,
       decoder_1_out13, decoder_1_out14, decoder_1_out15;
  wire [19:0] register_1_q, register_2_q, register_3_q, register_4_q, register_5_q, register_6_q,
       register_7_q, register_8_q, register_9_q, register_10_q, register_11_q, register_12_q, register_13_q,
       register_14_q, register_15_q, register_16_q;

  Decoder #(.select(4), .enable("false")) decoder_1 (
    .out0(decoder_1_out0), .out1(decoder_1_out1), .out2(decoder_1_out2), .out3(decoder_1_out3),
    .out4(decoder_1_out4), .out5(decoder_1_out5), .out6(decoder_1_out6), .out7(decoder_1_out7),
    .out8(decoder_1_out8), .out9(decoder_1_out9), .out10(decoder_1_out10), .out11(decoder_1_out11),
    .out12(decoder_1_out12), .out13(decoder_1_out13), .out14(decoder_1_out14), .out15(decoder_1_out15),
    .sel(which_reg));
  and and_1 (and_1_out, WE, decoder_1_out0);
  and and_2 (and_2_out, WE, decoder_1_out1);
  and and_3 (and_3_out, WE, decoder_1_out2);
  and and_4 (and_4_out, WE, decoder_1_out3);
  and and_5 (and_5_out, WE, decoder_1_out4);
  and and_6 (and_6_out, WE, decoder_1_out5);
  and and_7 (and_7_out, WE, decoder_1_out6);
  and and_8 (and_8_out, WE, decoder_1_out7);
  Register #(.width(20)) register_1 (.D(data_in), .en(and_1_out), .Q(register_1_q), .clk(clk));  // open: clr
  Register #(.width(20)) register_2 (.D(data_in), .en(and_2_out), .Q(register_2_q), .clk(clk));  // open: clr
  Register #(.width(20)) register_3 (.D(data_in), .en(and_3_out), .Q(register_3_q), .clk(clk));  // open: clr
  Register #(.width(20)) register_4 (.D(data_in), .en(and_4_out), .Q(register_4_q), .clk(clk));  // open: clr
  Register #(.width(20)) register_5 (.D(data_in), .en(and_5_out), .Q(register_5_q), .clk(clk));  // open: clr
  Register #(.width(20)) register_6 (.D(data_in), .en(and_6_out), .Q(register_6_q), .clk(clk));  // open: clr
  Register #(.width(20)) register_7 (.D(data_in), .en(and_7_out), .Q(register_7_q), .clk(clk));  // open: clr
  Register #(.width(20)) register_8 (.D(data_in), .en(and_8_out), .Q(register_8_q), .clk(clk));  // open: clr
  and and_9 (and_9_out, WE, decoder_1_out8);
  and and_10 (and_10_out, WE, decoder_1_out9);
  and and_11 (and_11_out, WE, decoder_1_out10);
  and and_12 (and_12_out, WE, decoder_1_out11);
  and and_13 (and_13_out, WE, decoder_1_out12);
  and and_14 (and_14_out, WE, decoder_1_out13);
  Register #(.width(20)) register_9 (.D(data_in), .en(and_9_out), .Q(register_9_q), .clk(clk));  // open: clr
  Register #(.width(20)) register_10 (.D(data_in), .en(and_10_out), .Q(register_10_q), .clk(clk));  // open: clr
  Register #(.width(20)) register_11 (.D(data_in), .en(and_11_out), .Q(register_11_q), .clk(clk));  // open: clr
  Register #(.width(20)) register_12 (.D(data_in), .en(and_12_out), .Q(register_12_q), .clk(clk));  // open: clr
  Register #(.width(20)) register_13 (.D(data_in), .en(and_13_out), .Q(register_13_q), .clk(clk));  // open: clr
  Register #(.width(20)) register_14 (.D(data_in), .en(and_14_out), .Q(register_14_q), .clk(clk));  // open: clr
  Register #(.width(20)) register_15 (.D(data_in), .en(and_15_out), .Q(register_15_q), .clk(clk));  // open: clr
  and and_15 (and_15_out, WE, decoder_1_out14);
  Register #(.width(20)) register_16 (.D(data_in), .en(and_16_out), .Q(register_16_q), .clk(clk));  // open: clr
  and and_16 (and_16_out, WE, decoder_1_out15);
  Multiplexer #(.select(4), .width(20), .enable("false")) multiplexer_1 (
    .in0(register_1_q), .in1(register_2_q), .in2(register_3_q), .in3(register_4_q), .in4(register_5_q),
    .in5(register_6_q), .in6(register_7_q), .in7(register_8_q), .in8(register_9_q), .in9(register_10_q),
    .in10(register_11_q), .in11(register_12_q), .in12(register_13_q), .in13(register_14_q),
    .in14(register_15_q), .in15(register_16_q), .out(ReadSrc1), .sel(adress_of_reg1));
  Multiplexer #(.select(4), .width(20), .enable("false")) multiplexer_2 (
    .in0(register_1_q), .in1(register_2_q), .in2(register_3_q), .in3(register_4_q), .in4(register_5_q),
    .in5(register_6_q), .in6(register_7_q), .in7(register_8_q), .in8(register_9_q), .in9(register_10_q),
    .in10(register_11_q), .in11(register_12_q), .in12(register_13_q), .in13(register_14_q),
    .in14(register_15_q), .in15(register_16_q), .out(ReadSrc2), .sel(address_of_reg2));
endmodule

module Alu (
  input  [19:0] input_a,
  input  [19:0] input_b,
  input  ImmOrReg,
  input  [7:0] Imm_Value,
  input  [1:0] AluOpcode,
  output [19:0] \output 
);

  wire [19:0] and_1_out, fulladder_1_output, multiplexer_1_out, or_1_out, xor_1_out;

  Multiplexer #(.width(20), .enable("false")) multiplexer_1 (
    .in0(input_b), .in1({{12{1'b0}}, Imm_Value}), .out(multiplexer_1_out), .sel(ImmOrReg));
  assign and_1_out = input_a & multiplexer_1_out;  // AND_Gate and_1, 20 bits wide
  assign xor_1_out = input_a ^ multiplexer_1_out;  // XOR_Gate xor_1, 20 bits wide
  assign or_1_out = input_a | multiplexer_1_out;  // OR_Gate or_1, 20 bits wide
  FullAdder fulladder_1 (.a(input_a), .b(multiplexer_1_out), .\output (fulladder_1_output));
  Multiplexer #(.select(2), .width(20), .enable("false")) multiplexer_2 (
    .in0(and_1_out), .in1(xor_1_out), .in2(or_1_out), .in3(fulladder_1_output), .out(\output ),
    .sel(AluOpcode));

  // Notes on the sheet:
  //   sign extension durumunu düşün
endmodule

module FullAdder (
  input  [19:0] a,
  input  [19:0] b,
  output [19:0] \output 
);

  wire and_1_out, and_2_out, and_3_out, and_4_out, and_5_out, and_6_out, and_7_out, and_8_out, and_9_out,
       and_10_out, and_11_out, and_12_out, and_13_out, and_14_out, and_15_out, and_16_out, and_17_out,
       and_18_out, and_19_out, and_20_out, and_21_out, and_22_out, and_23_out, and_24_out, and_25_out,
       and_26_out, and_27_out, and_28_out, and_29_out, and_30_out, and_31_out, and_32_out, and_33_out,
       and_34_out, and_35_out, and_36_out, and_37_out, and_38_out, or_1_out, or_2_out, or_3_out, or_4_out,
       or_5_out, or_6_out, or_7_out, or_8_out, or_9_out, or_10_out, or_11_out, or_12_out, or_13_out,
       or_14_out, or_15_out, or_16_out, or_17_out, or_18_out, or_19_out, xor_1_out, xor_3_out, xor_6_out,
       xor_7_out, xor_9_out, xor_11_out, xor_14_out, xor_15_out, xor_18_out, xor_19_out, xor_21_out,
       xor_23_out, xor_25_out, xor_27_out, xor_29_out, xor_31_out, xor_34_out, xor_35_out, xor_37_out,
       xor_39_out;

  xor xor_1 (xor_1_out, a[19], b[19]);
  xor xor_2 (\output [19], or_1_out, xor_1_out);
  and and_1 (and_1_out, a[18], b[18]);
  or or_1 (or_1_out, and_1_out, and_2_out);
  and and_2 (and_2_out, xor_3_out, or_2_out);
  xor xor_3 (xor_3_out, a[18], b[18]);
  xor xor_4 (\output [18], or_2_out, xor_3_out);
  and and_3 (and_3_out, a[17], b[17]);
  and and_4 (and_4_out, xor_6_out, or_3_out);
  or or_2 (or_2_out, and_3_out, and_4_out);
  xor xor_5 (\output [17], or_3_out, xor_6_out);
  xor xor_6 (xor_6_out, a[17], b[17]);
  and and_5 (and_5_out, a[16], b[16]);
  or or_3 (or_3_out, and_5_out, and_6_out);
  and and_6 (and_6_out, xor_7_out, or_4_out);
  xor xor_7 (xor_7_out, a[16], b[16]);
  xor xor_8 (\output [16], or_4_out, xor_7_out);
  and and_7 (and_7_out, a[15], b[15]);
  or or_4 (or_4_out, and_7_out, and_8_out);
  and and_8 (and_8_out, xor_9_out, or_5_out);
  xor xor_9 (xor_9_out, a[15], b[15]);
  xor xor_10 (\output [15], or_5_out, xor_9_out);
  and and_9 (and_9_out, a[14], b[14]);
  and and_10 (and_10_out, xor_11_out, or_6_out);
  or or_5 (or_5_out, and_9_out, and_10_out);
  xor xor_11 (xor_11_out, a[14], b[14]);
  xor xor_12 (\output [14], or_6_out, xor_11_out);
  and and_11 (and_11_out, a[13], b[13]);
  and and_12 (and_12_out, xor_14_out, or_7_out);
  or or_6 (or_6_out, and_11_out, and_12_out);
  xor xor_13 (\output [13], or_7_out, xor_14_out);
  xor xor_14 (xor_14_out, a[13], b[13]);
  and and_13 (and_13_out, a[12], b[12]);
  and and_14 (and_14_out, xor_15_out, or_8_out);
  or or_7 (or_7_out, and_13_out, and_14_out);
  xor xor_15 (xor_15_out, a[12], b[12]);
  xor xor_16 (\output [12], or_8_out, xor_15_out);
  and and_15 (and_15_out, a[11], b[11]);
  and and_16 (and_16_out, xor_18_out, or_9_out);
  or or_8 (or_8_out, and_15_out, and_16_out);
  xor xor_17 (\output [11], or_9_out, xor_18_out);
  xor xor_18 (xor_18_out, a[11], b[11]);
  and and_17 (and_17_out, a[10], b[10]);
  or or_9 (or_9_out, and_17_out, and_18_out);
  and and_18 (and_18_out, xor_19_out, or_10_out);
  xor xor_19 (xor_19_out, a[10], b[10]);
  xor xor_20 (\output [10], or_10_out, xor_19_out);
  and and_19 (and_19_out, a[9], b[9]);
  or or_10 (or_10_out, and_19_out, and_20_out);
  and and_20 (and_20_out, xor_21_out, or_11_out);
  xor xor_21 (xor_21_out, a[9], b[9]);
  xor xor_22 (\output [9], or_11_out, xor_21_out);
  and and_21 (and_21_out, a[8], b[8]);
  or or_11 (or_11_out, and_21_out, and_22_out);
  and and_22 (and_22_out, xor_23_out, or_12_out);
  xor xor_23 (xor_23_out, a[8], b[8]);
  xor xor_24 (\output [8], or_12_out, xor_23_out);
  and and_23 (and_23_out, a[7], b[7]);
  or or_12 (or_12_out, and_23_out, and_24_out);
  and and_24 (and_24_out, xor_25_out, or_13_out);
  xor xor_25 (xor_25_out, a[7], b[7]);
  xor xor_26 (\output [7], or_13_out, xor_25_out);
  and and_25 (and_25_out, a[6], b[6]);
  and and_26 (and_26_out, xor_27_out, or_14_out);
  or or_13 (or_13_out, and_25_out, and_26_out);
  xor xor_27 (xor_27_out, a[6], b[6]);
  xor xor_28 (\output [6], or_14_out, xor_27_out);
  and and_27 (and_27_out, a[5], b[5]);
  or or_14 (or_14_out, and_27_out, and_28_out);
  and and_28 (and_28_out, xor_29_out, or_15_out);
  xor xor_29 (xor_29_out, a[5], b[5]);
  xor xor_30 (\output [5], or_15_out, xor_29_out);
  and and_29 (and_29_out, a[4], b[4]);
  and and_30 (and_30_out, xor_31_out, or_16_out);
  or or_15 (or_15_out, and_29_out, and_30_out);
  xor xor_31 (xor_31_out, a[4], b[4]);
  xor xor_32 (\output [4], or_16_out, xor_31_out);
  and and_31 (and_31_out, a[3], b[3]);
  and and_32 (and_32_out, xor_34_out, or_17_out);
  or or_16 (or_16_out, and_31_out, and_32_out);
  xor xor_33 (\output [3], or_17_out, xor_34_out);
  xor xor_34 (xor_34_out, a[3], b[3]);
  and and_33 (and_33_out, a[2], b[2]);
  or or_17 (or_17_out, and_33_out, and_34_out);
  and and_34 (and_34_out, xor_35_out, or_18_out);
  xor xor_35 (xor_35_out, a[2], b[2]);
  xor xor_36 (\output [2], or_18_out, xor_35_out);
  and and_35 (and_35_out, a[1], b[1]);
  or or_18 (or_18_out, and_35_out, and_36_out);
  and and_36 (and_36_out, or_19_out, xor_37_out);
  xor xor_37 (xor_37_out, a[1], b[1]);
  xor xor_38 (\output [1], or_19_out, xor_37_out);
  and and_37 (and_37_out, a[0], b[0]);
  or or_19 (or_19_out, and_37_out, and_38_out);
  and and_38 (and_38_out, xor_39_out, 1'b0);
  xor xor_39 (xor_39_out, a[0], b[0]);
  xor xor_40 (\output [0], 1'b0, xor_39_out);

  // Notes on the sheet:
  //   a
  //   b
  //   carry_in
endmodule

module _5bitRegister (
  input  [4:0] Data,
  input  S0,
  input  clk,
  output [4:0] value
);

  wire multiplexer_1_out, multiplexer_2_out, multiplexer_3_out, multiplexer_4_out, multiplexer_5_out;

  Multiplexer #(.enable("false")) multiplexer_1 (.in0(Data[4]), .in1(value[4]), .out(multiplexer_1_out), .sel(S0));
  DFlipFlop dflipflop_1 (.in_1(multiplexer_1_out), .in_2(clk), .out_3(value[4]));
  Multiplexer #(.enable("false")) multiplexer_2 (.in0(Data[3]), .in1(value[3]), .out(multiplexer_2_out), .sel(S0));
  DFlipFlop dflipflop_2 (.in_1(multiplexer_2_out), .in_2(clk), .out_3(value[3]));
  Multiplexer #(.enable("false")) multiplexer_3 (.in0(Data[2]), .in1(value[2]), .out(multiplexer_3_out), .sel(S0));
  Multiplexer #(.enable("false")) multiplexer_4 (.in0(Data[1]), .in1(value[1]), .out(multiplexer_4_out), .sel(S0));
  DFlipFlop dflipflop_3 (.in_1(multiplexer_3_out), .in_2(clk), .out_3(value[2]));
  DFlipFlop dflipflop_4 (.in_1(multiplexer_4_out), .in_2(clk), .out_3(value[1]));
  Multiplexer #(.enable("false")) multiplexer_5 (.in0(Data[0]), .in1(value[0]), .out(multiplexer_5_out), .sel(S0));
  DFlipFlop dflipflop_5 (.in_1(multiplexer_5_out), .in_2(clk), .out_3(value[0]));
endmodule

module deneme (
);

  FullAdder fulladder_1 ();  // open: a, b, output
  Alu alu_1 ();  // open: input_a, input_b, output, Imm_Value, ImmOrReg, AluOpcode
  RegFile regfile_1 ();  // open: data_in, WE, ReadSrc1, ReadSrc2, which_reg, clk, adress_of_reg1, address_of_reg2
  RegFile regfile_2 ();  // open: data_in, WE, ReadSrc1, ReadSrc2, which_reg, clk, adress_of_reg1, address_of_reg2
  Alu alu_2 ();  // open: input_a, input_b, output, Imm_Value, ImmOrReg, AluOpcode
endmodule

module Datapath (
  input  in_1
);

  wire branchTruth, comparators_1_equal, comparators_1_greaterthan, comparators_1_lessthan, ImmOrReg,
       jumpCondi, not_1_out, PC_1_or_Relative, RegDataINcontrol, storeControl, ToNextIns, WE;
  wire [1:0] AluOpcode;
  wire [2:0] INSnzp;
  wire [3:0] destReg, src1, src2;
  wire [4:0] branchAddress;
  wire [7:0] immValue;
  wire [9:0] strLoad_Addresss;
  wire [15:0] jumpAddress;
  wire [19:0] alu_1_output, ins, multiplexer_1_out, pc_1_instruction, ram_1_data, regfile_1_readsrc1,
       regfile_1_readsrc2;

  PC pc_1 (
    .next_INS(ToNextIns), .\PC_1_OR_PC_RELATİVE (PC_1_or_Relative), .CLK(in_1),
    .instruction(pc_1_instruction), .jump_address(jumpAddress), .branch_address(branchAddress),
    .jump_condition(jumpCondi));
  ROM #(.addrWidth(20), .dataWidth(20)) rom_1 (.addr(pc_1_instruction), .data(ins));  // open: sel
  Control_Unit control_unit_1 (
    .instruction(ins), .destReg(destReg), .src1(src1), .src2(src2), .immValue(immValue),
    .ToNextIns_inPC(ToNextIns), .WE(WE), .ImmOrReg(ImmOrReg), .AluOpcode(AluOpcode), .clk(in_1),
    .str_load_address(strLoad_Addresss), .jump_address(jumpAddress), .branch_address(branchAddress),
    .nzp_values(INSnzp), .PC_JumpOrBranchAddress(jumpCondi), .branchtruthtest(branchTruth),
    .PC_1_OR_PC_relative(PC_1_or_Relative), .storeControl(storeControl), .RegDataINcontrol(RegDataINcontrol));  // open: opcode
  RegFile regfile_1 (
    .data_in(multiplexer_1_out), .WE(WE), .ReadSrc1(regfile_1_readsrc1), .ReadSrc2(regfile_1_readsrc2),
    .which_reg(destReg), .clk(in_1), .adress_of_reg1(src1), .address_of_reg2(src2));
  Comparators comparators_1 (
    .lessThan(comparators_1_lessthan), .equal(comparators_1_equal), .greaterThan(comparators_1_greaterthan),
    .a(regfile_1_readsrc1), .b(regfile_1_readsrc2));
  Multiplexer #(.width(20), .enable("false")) multiplexer_1 (
    .in0(alu_1_output), .in1(ram_1_data), .out(multiplexer_1_out), .sel(RegDataINcontrol));
  NZP nzp_1 (
    .N(INSnzp[2]), .Z(INSnzp[1]), .P(INSnzp[0]), .LT(comparators_1_lessthan), .EQ(comparators_1_equal),
    .GT(comparators_1_greaterthan), .BranchTruth(branchTruth));
  Alu alu_1 (
    .input_a(regfile_1_readsrc1), .input_b(regfile_1_readsrc2), .\output (alu_1_output),
    .Imm_Value(immValue), .ImmOrReg(ImmOrReg), .AluOpcode(AluOpcode));
  not not_1 (not_1_out, storeControl);
  RAM #(.addrWidth(10), .dataWidth(20), .bus("separate")) ram_1 (
    .addr(strLoad_Addresss), .din(regfile_1_readsrc1), .data(ram_1_data), .str(storeControl), .clk(in_1),
    .ld(not_1_out));  // open: sel, clr

  // Notes on the sheet:
  //   150114028
  //   contents of rom_1 (hex, n*v repeats v):
  //   f0013
endmodule

module Control_Unit (
  input  [19:0] instruction,
  input  clk,
  input  branchtruthtest,
  output [3:0] opcode,
  output [3:0] destReg,
  output RegDataINcontrol,
  output ToNextIns_inPC,
  output [3:0] src1,
  output WE,
  output PC_JumpOrBranchAddress,
  output [3:0] src2,
  output [7:0] immValue,
  output ImmOrReg,
  output storeControl,
  output [9:0] str_load_address,
  output [1:0] AluOpcode,
  output [15:0] jump_address,
  output [2:0] nzp_values,
  output PC_1_OR_PC_relative,
  output [4:0] branch_address
);

  wire and_1_out, and_2_out, and_3_out, and_4_out, and_5_out, decoder_1_out0, decoder_1_out4, decoder_1_out5,
       decoder_1_out9, decoder_1_out10, decoder_1_out11, or_1_out, or_2_out;
  wire [3:0] state_control_1_whichstate;

  Multiplexer #(.width(4), .enable("false")) multiplexer_1 (
    .in0(instruction[11:8]), .in1(instruction[15:12]), .out(src1), .sel(or_1_out));
  or or_1 (or_1_out, storeControl, decoder_1_out11);
  state_control state_control_1 (.opcode(instruction[19:16]), .clk(clk), .WhichState(state_control_1_whichstate));
  Decoder #(.select(4), .enable("false")) decoder_1 (
    .out0(decoder_1_out0), .out3(RegDataINcontrol), .out4(decoder_1_out4), .out5(decoder_1_out5),
    .out6(storeControl), .out8(PC_JumpOrBranchAddress), .out9(decoder_1_out9), .out10(decoder_1_out10),
    .out11(decoder_1_out11), .sel(state_control_1_whichstate));  // open: out1, out2, out7, out12, out13, out14, out15
  and and_1 (and_1_out, decoder_1_out11, branchtruthtest);
  or or_2 (or_2_out, decoder_1_out4, decoder_1_out5, decoder_1_out9, decoder_1_out10);
  or or_3 (PC_1_OR_PC_relative, PC_JumpOrBranchAddress, and_1_out);
  or or_4 (WE, RegDataINcontrol, decoder_1_out4, decoder_1_out5, decoder_1_out9, decoder_1_out10);
  and and_2 (and_2_out, decoder_1_out4, instruction[16]);
  and and_3 (and_3_out, decoder_1_out5, instruction[16]);
  and and_4 (and_4_out, decoder_1_out9, instruction[16]);
  and and_5 (and_5_out, decoder_1_out10, instruction[16]);
  AluCodeCreate alucodecreate_1 (.opcode(instruction[19:16]), .d(or_2_out), .alucode(AluOpcode));
  or or_5 (ImmOrReg, and_2_out, and_3_out, and_4_out, and_5_out);
  or or_6 (ToNextIns_inPC, decoder_1_out0, PC_1_OR_PC_relative);

  assign branch_address = instruction[7:3];
  assign destReg = instruction[15:12];
  assign immValue = instruction[7:0];
  assign jump_address = instruction[15:0];
  assign nzp_values = instruction[2:0];
  assign opcode = instruction[19:16];
  assign src2 = instruction[7:4];
  assign str_load_address = instruction[9:0];

  // Notes on the sheet:
  //   Imm test 
  //   0 yani fetch 1 pc de nextInst girecek
endmodule

module PC (
  input  [15:0] jump_address,
  input  jump_condition,
  input  [4:0] branch_address,
  input  \PC_1_OR_PC_RELATİVE ,
  input  next_INS,
  input  CLK,
  output [19:0] instruction
);

  wire [19:0] fulladder_1_output, fulladder_2_output, multiplexer_1_out, multiplexer_2_out,
       multiplexer_3_out, multiplexer_4_out, multiplexer_5_out;

  Multiplexer #(.width(20), .enable("false")) multiplexer_1 (
    .in0({4'b0000, jump_address}), .in1({4'b1111, jump_address}), .out(multiplexer_1_out),
    .sel(jump_address[15]));
  Multiplexer #(.width(20), .enable("false")) multiplexer_2 (
    .in0({{15{1'b0}}, branch_address}), .in1({{15{1'b1}}, branch_address}), .out(multiplexer_2_out),
    .sel(branch_address[4]));
  Multiplexer #(.width(20), .enable("false")) multiplexer_3 (
    .in0(multiplexer_2_out), .in1(multiplexer_1_out), .out(multiplexer_3_out), .sel(jump_condition));
  FullAdder fulladder_1 (.a(instruction), .b(20'h1), .\output (fulladder_1_output));
  FullAdder fulladder_2 (.a(multiplexer_3_out), .b(fulladder_1_output), .\output (fulladder_2_output));
  Multiplexer #(.width(20), .enable("false")) multiplexer_4 (
    .in0(instruction), .in1(multiplexer_5_out), .out(multiplexer_4_out), .sel(next_INS));
  Multiplexer #(.width(20), .enable("false")) multiplexer_5 (
    .in0(fulladder_1_output), .in1(fulladder_2_output), .out(multiplexer_5_out), .sel(\PC_1_OR_PC_RELATİVE ));
  Register #(.width(20)) register_1 (.D(multiplexer_4_out), .Q(instruction), .clk(CLK));  // open: en, clr

  // Notes on the sheet:
  //   branch address
  //   jumo address
  //   decoder 
  //   dan gelecek değer
  //   FETCH1 DE 1 OLACAK
  //   BRANCH YA DA JUMP DA 1 OLACAK
  //   inst memory e girecek değer
endmodule

module _20bitRegister (
  input  [19:0] \input ,
  input  SelectRegOp,
  input  clk,
  output [19:0] \output 
);

  _5bitRegister u_5bitregister_1 (.S0(SelectRegOp), .clk(clk), .value(\output [19:15]), .Data(\input [19:15]));
  _5bitRegister u_5bitregister_2 (.S0(SelectRegOp), .clk(clk), .value(\output [14:10]), .Data(\input [14:10]));
  _5bitRegister u_5bitregister_3 (.S0(SelectRegOp), .clk(clk), .value(\output [9:5]), .Data(\input [9:5]));
  _5bitRegister u_5bitregister_4 (.S0(SelectRegOp), .clk(clk), .value(\output [4:0]), .Data(\input [4:0]));
endmodule

module state_control (
  input  [3:0] opcode,
  input  clk,
  output [3:0] WhichState
);

  wire [3:0] register_1_q;

  Register #(.width(4)) register_1 (.D(WhichState), .Q(register_1_q), .clk(clk));  // open: en, clr
  // stateLogic_main main_1: pin names not known; wires that end beside it: opcode, register_1_q, WhichState
endmodule

module AluCodeCreate (
  input  [3:0] opcode,
  input  d,
  output [1:0] alucode
);

  wire and_1_out, and_2_out;

  and a1 (alucode[1], ~opcode[3], ~opcode[1], d);  // AND_Gate
  and and_1 (and_1_out, ~opcode[3], opcode[2], opcode[1], d);  // AND_Gate
  and and_2 (and_2_out, ~opcode[3], ~opcode[2], ~opcode[1], d);  // AND_Gate
  or a0 (alucode[0], and_1_out, and_2_out);
endmodule

module branchCondition (
  input  [2:0] nzp,
  input  [19:0] a,
  input  [19:0] b,
  output branchTruthTest
);

  wire comparator_1_eq, comparator_1_gt, comparator_1_lt, xnor_1_out, xnor_2_out, xnor_3_out;

  Comparator_part #(.width(20), .mode("unsigned")) comparator_1 (
    .a(a), .b(b), .gt(comparator_1_gt), .eq(comparator_1_eq), .lt(comparator_1_lt));
  xnor xnor_1 (xnor_1_out, nzp[0], comparator_1_gt);
  xnor xnor_2 (xnor_2_out, nzp[1], comparator_1_eq);
  and and_1 (branchTruthTest, xnor_1_out, xnor_2_out, xnor_3_out);
  xnor xnor_3 (xnor_3_out, nzp[2], comparator_1_lt);
endmodule

module Comparator (
  input  prev_lt,
  input  prev_eq,
  input  prev__gt,
  input  a,
  input  b,
  output lt,
  output eq,
  output gt
);

  wire and_1_out, and_2_out, and_3_out, and_5_out, xnor_1_out;

  and and_1 (and_1_out, ~a, b);  // AND_Gate
  xnor xnor_1 (xnor_1_out, a, b);
  and and_2 (and_2_out, a, ~b);  // AND_Gate
  and and_3 (and_3_out, prev_eq, and_1_out);
  and and_4 (eq, prev_eq, xnor_1_out);
  and and_5 (and_5_out, prev_eq, and_2_out);
  or or_1 (lt, and_3_out, prev_lt);
  or or_2 (gt, prev__gt, and_5_out);
endmodule

module Comparators (
  input  [19:0] a,
  input  [19:0] b,
  output lessThan,
  output equal,
  output greaterThan
);

  wire and_1_out, and_2_out, comparator_1_eq, comparator_1_gt, comparator_1_lt, comparator_2_eq,
       comparator_2_gt, comparator_2_lt, comparator_3_eq, comparator_3_gt, comparator_3_lt, comparator_4_eq,
       comparator_4_gt, comparator_4_lt, comparator_5_eq, comparator_5_gt, comparator_5_lt, comparator_6_eq,
       comparator_6_gt, comparator_6_lt, comparator_7_eq, comparator_7_gt, comparator_7_lt, comparator_8_eq,
       comparator_8_gt, comparator_8_lt, comparator_9_eq, comparator_9_gt, comparator_9_lt, comparator_10_eq,
       comparator_10_gt, comparator_10_lt, comparator_11_eq, comparator_11_gt, comparator_11_lt,
       comparator_12_eq, comparator_12_gt, comparator_12_lt, comparator_13_eq, comparator_13_gt,
       comparator_13_lt, comparator_14_eq, comparator_14_gt, comparator_14_lt, comparator_15_eq,
       comparator_15_gt, comparator_15_lt, comparator_16_eq, comparator_16_gt, comparator_16_lt,
       comparator_17_eq, comparator_17_gt, comparator_17_lt, comparator_18_eq, comparator_18_gt,
       comparator_18_lt, xnor_1_out;

  and and_1 (and_1_out, a[19], ~b[19]);  // AND_Gate
  xnor xnor_1 (xnor_1_out, a[19], b[19]);
  and and_2 (and_2_out, ~a[19], b[19]);  // AND_Gate
  Comparator comparator_1 (
    .lt(comparator_1_lt), .eq(comparator_1_eq), .gt(comparator_1_gt), .a(a[18]), .b(b[18]),
    .prev_lt(and_1_out), .prev_eq(xnor_1_out), .prev__gt(and_2_out));
  Comparator comparator_2 (
    .lt(comparator_2_lt), .eq(comparator_2_eq), .gt(comparator_2_gt), .a(a[17]), .b(b[17]),
    .prev_lt(comparator_1_lt), .prev_eq(comparator_1_eq), .prev__gt(comparator_1_gt));
  Comparator comparator_3 (
    .lt(comparator_3_lt), .eq(comparator_3_eq), .gt(comparator_3_gt), .a(a[16]), .b(b[16]),
    .prev_lt(comparator_2_lt), .prev_eq(comparator_2_eq), .prev__gt(comparator_2_gt));
  Comparator comparator_4 (
    .lt(comparator_4_lt), .eq(comparator_4_eq), .gt(comparator_4_gt), .a(a[15]), .b(b[15]),
    .prev_lt(comparator_3_lt), .prev_eq(comparator_3_eq), .prev__gt(comparator_3_gt));
  Comparator comparator_5 (
    .lt(comparator_5_lt), .eq(comparator_5_eq), .gt(comparator_5_gt), .a(a[14]), .b(b[14]),
    .prev_lt(comparator_4_lt), .prev_eq(comparator_4_eq), .prev__gt(comparator_4_gt));
  Comparator comparator_6 (
    .lt(comparator_6_lt), .eq(comparator_6_eq), .gt(comparator_6_gt), .a(a[13]), .b(b[13]),
    .prev_lt(comparator_5_lt), .prev_eq(comparator_5_eq), .prev__gt(comparator_5_gt));
  Comparator comparator_7 (
    .lt(comparator_7_lt), .eq(comparator_7_eq), .gt(comparator_7_gt), .a(a[12]), .b(b[12]),
    .prev_lt(comparator_6_lt), .prev_eq(comparator_6_eq), .prev__gt(comparator_6_gt));
  Comparator comparator_8 (
    .lt(comparator_8_lt), .eq(comparator_8_eq), .gt(comparator_8_gt), .a(a[11]), .b(b[11]),
    .prev_lt(comparator_7_lt), .prev_eq(comparator_7_eq), .prev__gt(comparator_7_gt));
  Comparator comparator_9 (
    .lt(comparator_9_lt), .eq(comparator_9_eq), .gt(comparator_9_gt), .a(a[10]), .b(b[10]),
    .prev_lt(comparator_8_lt), .prev_eq(comparator_8_eq), .prev__gt(comparator_8_gt));
  Comparator comparator_10 (
    .lt(comparator_10_lt), .eq(comparator_10_eq), .gt(comparator_10_gt), .a(a[9]), .b(b[9]),
    .prev_lt(comparator_9_lt), .prev_eq(comparator_9_eq), .prev__gt(comparator_9_gt));
  Comparator comparator_11 (
    .lt(comparator_11_lt), .eq(comparator_11_eq), .gt(comparator_11_gt), .a(a[8]), .b(b[8]),
    .prev_lt(comparator_10_lt), .prev_eq(comparator_10_eq), .prev__gt(comparator_10_gt));
  Comparator comparator_12 (
    .lt(comparator_12_lt), .eq(comparator_12_eq), .gt(comparator_12_gt), .a(a[7]), .b(b[7]),
    .prev_lt(comparator_11_lt), .prev_eq(comparator_11_eq), .prev__gt(comparator_11_gt));
  Comparator comparator_13 (
    .lt(comparator_13_lt), .eq(comparator_13_eq), .gt(comparator_13_gt), .a(a[6]), .b(b[6]),
    .prev_lt(comparator_12_lt), .prev_eq(comparator_12_eq), .prev__gt(comparator_12_gt));
  Comparator comparator_14 (
    .lt(comparator_14_lt), .eq(comparator_14_eq), .gt(comparator_14_gt), .a(a[5]), .b(b[5]),
    .prev_lt(comparator_13_lt), .prev_eq(comparator_13_eq), .prev__gt(comparator_13_gt));
  Comparator comparator_15 (
    .lt(comparator_15_lt), .eq(comparator_15_eq), .gt(comparator_15_gt), .a(a[4]), .b(b[4]),
    .prev_lt(comparator_14_lt), .prev_eq(comparator_14_eq), .prev__gt(comparator_14_gt));
  Comparator comparator_16 (
    .lt(comparator_16_lt), .eq(comparator_16_eq), .gt(comparator_16_gt), .a(a[3]), .b(b[3]),
    .prev_lt(comparator_15_lt), .prev_eq(comparator_15_eq), .prev__gt(comparator_15_gt));
  Comparator comparator_17 (
    .lt(comparator_17_lt), .eq(comparator_17_eq), .gt(comparator_17_gt), .a(a[2]), .b(b[2]),
    .prev_lt(comparator_16_lt), .prev_eq(comparator_16_eq), .prev__gt(comparator_16_gt));
  Comparator comparator_18 (
    .lt(comparator_18_lt), .eq(comparator_18_eq), .gt(comparator_18_gt), .a(a[1]), .b(b[1]),
    .prev_lt(comparator_17_lt), .prev_eq(comparator_17_eq), .prev__gt(comparator_17_gt));
  Comparator comparator_19 (
    .lt(lessThan), .eq(equal), .gt(greaterThan), .a(a[0]), .b(b[0]), .prev_lt(comparator_18_lt),
    .prev_eq(comparator_18_eq), .prev__gt(comparator_18_gt));

  // Notes on the sheet:
  //   lessThan
  //   equal
  //   greater than
endmodule

module NZP (
  input  N,
  input  Z,
  input  P,
  input  LT,
  input  EQ,
  input  GT,
  output BranchTruth
);

  wire and_1_out, and_2_out, and_3_out, xnor_1_out, xnor_2_out, xnor_3_out;

  xnor xnor_1 (xnor_1_out, N, LT);
  xnor xnor_2 (xnor_2_out, Z, EQ);
  xnor xnor_3 (xnor_3_out, P, GT);
  and and_1 (and_1_out, xnor_1_out, xnor_2_out, xnor_3_out);
  and and_2 (and_2_out, ~N, Z, P, ~LT);  // AND_Gate
  or or_1 (BranchTruth, and_1_out, and_2_out, and_3_out);
  and and_3 (and_3_out, N, Z, ~P, ~GT);  // AND_Gate

  // Notes on the sheet:
  //   BEQ,BLT,BGT
  //   BGE
  //   BLE
endmodule
