// Logisim project ProcessorNamık.circ as structural Verilog: 24 circuits, main circuit SR Latch
module SR_Latch (
  input  S__set,
  input  R__reset,
  output Q
);

  wire nor_1_out;

  nor nor_1 (nor_1_out, S__set, Q);
  nor nor_2 (Q, nor_1_out, R__reset);
endmodule

module D_Latch (
  input  D,
  input  clk,
  output Q
);

  wire and_1_out, and_2_out, not_1_out;

  not not_1 (not_1_out, D);
  and and_1 (and_1_out, D, clk);
  and and_2 (and_2_out, clk, not_1_out);
  SR_Latch SR_Latch (.S__set(and_1_out), .R__reset(and_2_out), .Q(Q));
endmodule

module D_Flip_Flop (
  input  D,
  input  clk,
  output Q
);

  wire D_Latch__master_q, not_1_out;

  not not_1 (not_1_out, clk);
  D_Latch D_Latch__master (.D(D), .clk(not_1_out), .Q(D_Latch__master_q));
  D_Latch D_Latch__servant (.D(D_Latch__master_q), .clk(clk), .Q(Q));
endmodule

// 2 R
module _2_bit_Register (
  input  I1,
  input  I0,
  input  clk,
  output Q1,
  output Q0
);

  D_Flip_Flop Flip_Flop (.D(I1), .clk(clk), .Q(Q1));
  D_Flip_Flop Flip_Flop_2 (.D(I0), .clk(clk), .Q(Q0));
endmodule

// 4 R
module _4_bit_Register (
  input  I3,
  input  I2,
  input  I1,
  input  I0,
  input  clk,
  output Q3,
  output Q2,
  output Q1,
  output Q0
);

  _2_bit_Register u_2_bit_register_1 (.clk(clk), .I1(I3), .I0(I2), .Q1(Q3), .Q0(Q2));
  _2_bit_Register u_2_bit_register_2 (.clk(clk), .I1(I1), .I0(I0), .Q1(Q1), .Q0(Q0));
endmodule

// 8 R
module _8_bit_Register (
  input  I7,
  input  I6,
  input  I5,
  input  I4,
  input  I3,
  input  I2,
  input  I1,
  input  I0,
  input  clk,
  output Q7,
  output Q6,
  output Q5,
  output Q4,
  output Q3,
  output Q2,
  output Q1,
  output Q0
);

  _4_bit_Register u_4_bit_register_1 (
    .clk(clk), .I3(I7), .I2(I6), .I1(I5), .I0(I4), .Q3(Q7), .Q2(Q6), .Q1(Q5), .Q0(Q4));
  _4_bit_Register u_4_bit_register_2 (
    .clk(clk), .I3(I3), .I2(I2), .I1(I1), .I0(I0), .Q3(Q3), .Q2(Q2), .Q1(Q1), .Q0(Q0));
endmodule

module _12_bit_Register (
  input  I11,
  input  I10,
  input  I9,
  input  I8,
  input  I7,
  input  I6,
  input  I5,
  input  I4,
  input  I3,
  input  I2,
  input  I1,
  input  I0,
  input  clk,
  output Q11,
  output Q10,
  output Q9,
  output Q8,
  output Q7,
  output Q6,
  output Q5,
  output Q4,
  output Q3,
  output Q2,
  output Q1,
  output Q0
);

  _8_bit_Register u_8_bit_register_1 (
    .clk(clk), .I7(I11), .I6(I10), .I5(I9), .I4(I8), .I3(I7), .I2(I6), .I1(I5), .I0(I4), .Q7(Q11), .Q6(Q10),
    .Q5(Q9), .Q4(Q8), .Q3(Q7), .Q2(Q6), .Q1(Q5), .Q0(Q4));
  _4_bit_Register u_4_bit_register_1 (
    .clk(clk), .I3(I3), .I2(I2), .I1(I1), .I0(I0), .Q3(Q3), .Q2(Q2), .Q1(Q1), .Q0(Q0));
endmodule

module _16_bit_Register (
  input  I15,
  input  I14,
  input  I13,
  input  I12,
  input  I11,
  input  I10,
  input  I9,
  input  I8,
  input  I7,
  input  I6,
  input  I5,
  input  I4,
  input  I3,
  input  I2,
  input  I1,
  input  I0,
  input  clk,
  output Q15,
  output Q14,
  output Q13,
  output Q12,
  output Q11,
  output Q10,
  output Q9,
  output Q8,
  output Q7,
  output Q6,
  output Q5,
  output Q4,
  output Q3,
  output Q2,
  output Q1,
  output Q0
);

  _8_bit_Register u_8_bit_register_1 (
    .clk(clk), .I7(I15), .I6(I14), .I5(I13), .I4(I12), .I3(I11), .I2(I10), .I1(I9), .I0(I8), .Q7(Q15),
    .Q6(Q14), .Q5(Q13), .Q4(Q12), .Q3(Q11), .Q2(Q10), .Q1(Q9), .Q0(Q8));
  _8_bit_Register u_8_bit_register_2 (
    .clk(clk), .I7(I7), .I6(I6), .I5(I5), .I4(I4), .I3(I3), .I2(I2), .I1(I1), .I0(I0), .Q7(Q7), .Q6(Q6),
    .Q5(Q5), .Q4(Q4), .Q3(Q3), .Q2(Q2), .Q1(Q1), .Q0(Q0));
endmodule

// R F
module Register_File (
  input  [3:0] read_register1,
  input  [3:0] read_register2,
  input  [3:0] write_register,
  input  [15:0] write_value,
  input  write,
  input  clk,
  output [15:0] output1,
  output [15:0] output2
);

  wire decoder_1_out0, decoder_1_out1, decoder_1_out2, decoder_1_out3, decoder_1_out4, decoder_1_out5,
       decoder_1_out6, decoder_1_out7, decoder_1_out8, decoder_1_out9, decoder_1_out10, decoder_1_out11,
       decoder_1_out12, decoder_1_out13, decoder_1_out14, decoder_1_out15, decoder_2_out0, decoder_2_out1,
       decoder_2_out2, decoder_2_out3, decoder_2_out4, decoder_2_out5, decoder_2_out6, decoder_2_out7,
       decoder_2_out8, decoder_2_out9, decoder_2_out10, decoder_2_out11, decoder_2_out12, decoder_2_out13,
       decoder_2_out14, decoder_2_out15, decoder_3_out0, decoder_3_out1, decoder_3_out2, decoder_3_out3,
       decoder_3_out4, decoder_3_out5, decoder_3_out6, decoder_3_out7, decoder_3_out8, decoder_3_out9,
       decoder_3_out10, decoder_3_out11, decoder_3_out12, decoder_3_out13, decoder_3_out14, decoder_3_out15,
       not_1_out;
  wire [15:0] R0_q, R1_q, R2_q, R3_q, R4_q, R5_q, R6_q, R7_q, R8_q, R9_q, R10_q, R11_q, R12_q, R13_q, R14_q,
       R15_q;

  Decoder #(.select(4), .disabled(0)) decoder_1 (
    .out0(decoder_1_out0), .out1(decoder_1_out1), .out2(decoder_1_out2), .out3(decoder_1_out3),
    .out4(decoder_1_out4), .out5(decoder_1_out5), .out6(decoder_1_out6), .out7(decoder_1_out7),
    .out8(decoder_1_out8), .out9(decoder_1_out9), .out10(decoder_1_out10), .out11(decoder_1_out11),
    .out12(decoder_1_out12), .out13(decoder_1_out13), .out14(decoder_1_out14), .out15(decoder_1_out15),
    .sel(read_register1));  // open: en
  Decoder #(.select(4), .disabled(0)) decoder_2 (
    .out0(decoder_2_out0), .out1(decoder_2_out1), .out2(decoder_2_out2), .out3(decoder_2_out3),
    .out4(decoder_2_out4), .out5(decoder_2_out5), .out6(decoder_2_out6), .out7(decoder_2_out7),
    .out8(decoder_2_out8), .out9(decoder_2_out9), .out10(decoder_2_out10), .out11(decoder_2_out11),
    .out12(decoder_2_out12), .out13(decoder_2_out13), .out14(decoder_2_out14), .out15(decoder_2_out15),
    .sel(read_register2));  // open: en
  not not_1 (not_1_out, write);
  Decoder #(.select(4), .disabled(0)) decoder_3 (
    .out0(decoder_3_out0), .out1(decoder_3_out1), .out2(decoder_3_out2), .out3(decoder_3_out3),
    .out4(decoder_3_out4), .out5(decoder_3_out5), .out6(decoder_3_out6), .out7(decoder_3_out7),
    .out8(decoder_3_out8), .out9(decoder_3_out9), .out10(decoder_3_out10), .out11(decoder_3_out11),
    .out12(decoder_3_out12), .out13(decoder_3_out13), .out14(decoder_3_out14), .out15(decoder_3_out15),
    .sel(write_register));  // open: en
  Register #(.width(16)) R0 (.D(write_value), .en(decoder_3_out0), .Q(R0_q), .clk(clk));  // open: clr
  Register #(.width(16)) R1 (.D(write_value), .en(decoder_3_out1), .Q(R1_q), .clk(clk));  // open: clr
  Register #(.width(16)) R2 (.D(write_value), .en(decoder_3_out2), .Q(R2_q), .clk(clk));  // open: clr
  Register #(.width(16)) R3 (.D(write_value), .en(decoder_3_out3), .Q(R3_q), .clk(clk));  // open: clr
  Register #(.width(16)) R4 (.D(write_value), .en(decoder_3_out4), .Q(R4_q), .clk(clk));  // open: clr
  Register #(.width(16)) R5 (.D(write_value), .en(decoder_3_out5), .Q(R5_q), .clk(clk));  // open: clr
  Register #(.width(16)) R6 (.D(write_value), .en(decoder_3_out6), .Q(R6_q), .clk(clk));  // open: clr
  Register #(.width(16)) R7 (.D(write_value), .en(decoder_3_out7), .Q(R7_q), .clk(clk));  // open: clr
  assign output1 = decoder_1_out0 ? R0_q : 16'bz;  // Controlled_Buffer controlled_buffer_1
  assign output2 = decoder_2_out0 ? R0_q : 16'bz;  // Controlled_Buffer controlled_buffer_2
  assign output1 = decoder_1_out1 ? R1_q : 16'bz;  // Controlled_Buffer controlled_buffer_3
  assign output2 = decoder_2_out1 ? R1_q : 16'bz;  // Controlled_Buffer controlled_buffer_4
  assign output1 = decoder_1_out2 ? R2_q : 16'bz;  // Controlled_Buffer controlled_buffer_5
  assign output2 = decoder_2_out2 ? R2_q : 16'bz;  // Controlled_Buffer controlled_buffer_6
  assign output1 = decoder_1_out3 ? R3_q : 16'bz;  // Controlled_Buffer controlled_buffer_7
  assign output2 = decoder_2_out3 ? R3_q : 16'bz;  // Controlled_Buffer controlled_buffer_8
  assign output1 = decoder_1_out4 ? R4_q : 16'bz;  // Controlled_Buffer controlled_buffer_9
  assign output2 = decoder_2_out4 ? R4_q : 16'bz;  // Controlled_Buffer controlled_buffer_10
  assign output1 = decoder_1_out5 ? R5_q : 16'bz;  // Controlled_Buffer controlled_buffer_11
  assign output2 = decoder_2_out5 ? R5_q : 16'bz;  // Controlled_Buffer controlled_buffer_12
  assign output1 = decoder_1_out6 ? R6_q : 16'bz;  // Controlled_Buffer controlled_buffer_13
  assign output2 = decoder_2_out6 ? R6_q : 16'bz;  // Controlled_Buffer controlled_buffer_14
  assign output1 = decoder_1_out7 ? R7_q : 16'bz;  // Controlled_Buffer controlled_buffer_15
  assign output2 = decoder_2_out7 ? R7_q : 16'bz;  // Controlled_Buffer controlled_buffer_16
  Register #(.width(16)) R8 (.D(write_value), .en(decoder_3_out8), .Q(R8_q), .clk(clk));  // open: clr
  Register #(.width(16)) R9 (.D(write_value), .en(decoder_3_out9), .Q(R9_q), .clk(clk));  // open: clr
  Register #(.width(16)) R10 (.D(write_value), .en(decoder_3_out10), .Q(R10_q), .clk(clk));  // open: clr
  Register #(.width(16)) R11 (.D(write_value), .en(decoder_3_out11), .Q(R11_q), .clk(clk));  // open: clr
  Register #(.width(16)) R12 (.D(write_value), .en(decoder_3_out12), .Q(R12_q), .clk(clk));  // open: clr
  Register #(.width(16)) R13 (.D(write_value), .en(decoder_3_out13), .Q(R13_q), .clk(clk));  // open: clr
  Register #(.width(16)) R14 (.D(write_value), .en(decoder_3_out14), .Q(R14_q), .clk(clk));  // open: clr
  Register #(.width(16)) R15 (.D(write_value), .en(decoder_3_out15), .Q(R15_q), .clk(clk));  // open: clr
  assign output1 = decoder_1_out8 ? R8_q : 16'bz;  // Controlled_Buffer controlled_buffer_17
  assign output2 = decoder_2_out8 ? R8_q : 16'bz;  // Controlled_Buffer controlled_buffer_18
  assign output1 = decoder_1_out9 ? R9_q : 16'bz;  // Controlled_Buffer controlled_buffer_19
  assign output2 = decoder_2_out9 ? R9_q : 16'bz;  // Controlled_Buffer controlled_buffer_20
  assign output1 = decoder_1_out10 ? R10_q : 16'bz;  // Controlled_Buffer controlled_buffer_21
  assign output2 = decoder_2_out10 ? R10_q : 16'bz;  // Controlled_Buffer controlled_buffer_22
  assign output1 = decoder_1_out11 ? R11_q : 16'bz;  // Controlled_Buffer controlled_buffer_23
  assign output2 = decoder_2_out11 ? R11_q : 16'bz;  // Controlled_Buffer controlled_buffer_24
  assign output1 = decoder_1_out12 ? R12_q : 16'bz;  // Controlled_Buffer controlled_buffer_25
  assign output2 = decoder_2_out12 ? R12_q : 16'bz;  // Controlled_Buffer controlled_buffer_26
  assign output1 = decoder_1_out13 ? R13_q : 16'bz;  // Controlled_Buffer controlled_buffer_27
  assign output2 = decoder_2_out13 ? R13_q : 16'bz;  // Controlled_Buffer controlled_buffer_28
  assign output1 = decoder_1_out14 ? R14_q : 16'bz;  // Controlled_Buffer controlled_buffer_29
  assign output2 = decoder_2_out14 ? R14_q : 16'bz;  // Controlled_Buffer controlled_buffer_30
  assign output1 = decoder_1_out15 ? R15_q : 16'bz;  // Controlled_Buffer controlled_buffer_31
  assign output2 = decoder_2_out15 ? R15_q : 16'bz;  // Controlled_Buffer controlled_buffer_32
endmodule

// HA
module Half_Adder (
  input  a,
  input  b,
  output carry_out,
  output sum
);

  and and_1 (carry_out, b, a);
  xor xor_1 (sum, b, a);
endmodule

// FA
module Full_Adder (
  input  a,
  input  b,
  input  carry_in,
  output carry_out,
  output sum
);

  wire half_adder_1_carry_out, half_adder_1_sum, half_adder_2_carry_out;

  Half_Adder half_adder_1 (.a(a), .b(b), .carry_out(half_adder_1_carry_out), .sum(half_adder_1_sum));
  Half_Adder half_adder_2 (.a(half_adder_1_sum), .b(carry_in), .carry_out(half_adder_2_carry_out), .sum(sum));
  or or_1 (carry_out, half_adder_1_carry_out, half_adder_2_carry_out);
endmodule

// 4 A
module _4_bit_Adder (
  input  [3:0] a,
  input  [3:0] b,
  input  carry_in,
  output carry_out,
  output [3:0] \output 
);

  wire full_adder_1_carry_out, full_adder_2_carry_out, full_adder_3_carry_out;

  Full_Adder full_adder_1 (
    .a(a[0]), .b(b[0]), .carry_in(carry_in), .carry_out(full_adder_1_carry_out), .sum(\output [0]));
  Full_Adder full_adder_2 (
    .a(a[1]), .b(b[1]), .carry_in(full_adder_1_carry_out), .carry_out(full_adder_2_carry_out),
    .sum(\output [1]));
  Full_Adder full_adder_3 (
    .a(a[2]), .b(b[2]), .carry_in(full_adder_2_carry_out), .carry_out(full_adder_3_carry_out),
    .sum(\output [2]));
  Full_Adder full_adder_4 (
    .a(a[3]), .b(b[3]), .carry_in(full_adder_3_carry_out), .carry_out(carry_out), .sum(\output [3]));
endmodule

// 8 A
module _8_bit_Adder (
  input  [7:0] a,
  input  [7:0] b,
  input  carry_in,
  output carry_out,
  output [7:0] out_5
);

  wire n4_bit_adder_1_carry_out;

  _4_bit_Adder u_4_bit_adder_1 (
    .a(a[3:0]), .b(b[3:0]), .carry_in(carry_in), .carry_out(n4_bit_adder_1_carry_out), .\output (out_5[3:0]));
  _4_bit_Adder u_4_bit_adder_2 (
    .a(a[7:4]), .b(b[7:4]), .carry_in(n4_bit_adder_1_carry_out), .carry_out(carry_out), .\output (out_5[7:4]));
endmodule

// 16 A
module _16_bit_Adder (
  input  [15:0] a,
  input  [15:0] b,
  input  carry_in,
  output carry_out,
  output [15:0] \output 
);

  wire n8_bit_adder_1_carry_out;

  _8_bit_Adder u_8_bit_adder_1 (
    .a(a[7:0]), .b(b[7:0]), .carry_in(carry_in), .carry_out(n8_bit_adder_1_carry_out), .out_5(\output [7:0]));
  _8_bit_Adder u_8_bit_adder_2 (
    .a(a[15:8]), .b(b[15:8]), .carry_in(n8_bit_adder_1_carry_out), .carry_out(carry_out),
    .out_5(\output [15:8]));
endmodule

module ALU (
  input  [15:0] a,
  input  [15:0] b,
  input  ALUand,
  input  ALUadd,
  output [15:0] \output 
);

  wire and_2_out, not_1_out;
  wire [15:0] and_1_out, n16_bit_adder_1_output;

  not not_1 (not_1_out, ALUand);
  assign and_1_out = b & a;  // AND_Gate and_1, 16 bits wide
  and and_2 (and_2_out, not_1_out, ALUadd);
  _16_bit_Adder u_16_bit_adder_1 (.a(a), .b(b), .carry_in(1'b0), .\output (n16_bit_adder_1_output));  // open: carry_out
  Multiplexer #(.width(16)) multiplexer_1 (
    .in0(and_1_out), .in1(n16_bit_adder_1_output), .out(\output ), .sel(and_2_out));  // open: en
endmodule

// C U
module Control_Unit (
  input  [3:0] instruction,
  output dataMemRead,
  output dataMemWrite,
  output regWrite,
  output immediate,
  output ALUand,
  output ALUadd,
  output comparator,
  output PCselect
);

  wire decoder_1_out0, decoder_1_out1, decoder_1_out2, decoder_1_out3, decoder_1_out7, decoder_1_out8,
       decoder_1_out9, decoder_1_out10, decoder_1_out11, decoder_1_out12;

  Decoder #(.select(4)) decoder_1 (
    .out0(decoder_1_out0), .out1(decoder_1_out1), .out2(decoder_1_out2), .out3(decoder_1_out3),
    .out4(dataMemRead), .out5(dataMemWrite), .out6(comparator), .out7(decoder_1_out7), .out8(decoder_1_out8),
    .out9(decoder_1_out9), .out10(decoder_1_out10), .out11(decoder_1_out11), .out12(decoder_1_out12),
    .sel(instruction));  // open: out13, out14, out15, en
  or u_regWrite (regWrite, decoder_1_out0, decoder_1_out1, decoder_1_out2, decoder_1_out3, dataMemRead);
  or u_ALUand (ALUand, decoder_1_out2, decoder_1_out3);
  or u_ALUadd (ALUadd, decoder_1_out0, decoder_1_out1);
  or u_PCselect (PCselect, decoder_1_out7, decoder_1_out8, decoder_1_out9, decoder_1_out10, decoder_1_out11, decoder_1_out12);
  or imm (immediate, decoder_1_out3, decoder_1_out1);
endmodule

module CPU (
);

  wire and_1_out, CF_q, clock_1_out, control_unit_1_aluadd, control_unit_1_aluand, control_unit_1_comparator,
       control_unit_1_datamemread, control_unit_1_datamemwrite, control_unit_1_immediate,
       control_unit_1_pcselect, control_unit_1_regwrite, flag_unit_1_cf, flag_unit_1_zf, jump_unit_1_jumpok,
       or_1_out, ZF_q;
  wire [3:0] multiplexer_3_out;
  wire [11:0] bit_extender_3_out, multiplexer_1_out, n12_bit_adder_1_output, PC_q;
  wire [15:0] alu_1_output, bit_extender_1_out, bit_extender_2_out, multiplexer_2_out, multiplexer_4_out,
       multiplexer_5_out, ram_1_data, register_file_1_output1, register_file_1_output2, rom_1_data;

  Multiplexer #(.width(12)) multiplexer_1 (
    .in0(12'h1), .in1(rom_1_data[11:0]), .out(multiplexer_1_out), .sel(and_1_out));  // open: en
  _12_bit_Adder u_12_bit_adder_1 (.a(multiplexer_1_out), .b(PC_q), .\output (n12_bit_adder_1_output));
  and and_1 (and_1_out, control_unit_1_pcselect, jump_unit_1_jumpok);
  Register #(.width(12)) PC (.D(n12_bit_adder_1_output), .Q(PC_q), .clk(clock_1_out));  // open: en, clr
  ROM #(.addrWidth(12), .dataWidth(16)) rom_1 (.addr(PC_q), .data(rom_1_data));  // open: sel
  Clock clock_1 (.out(clock_1_out));
  Control_Unit control_unit_1 (
    .instruction(rom_1_data[15:12]), .dataMemRead(control_unit_1_datamemread),
    .dataMemWrite(control_unit_1_datamemwrite), .regWrite(control_unit_1_regwrite),
    .immediate(control_unit_1_immediate), .ALUand(control_unit_1_aluand), .ALUadd(control_unit_1_aluadd),
    .comparator(control_unit_1_comparator), .PCselect(control_unit_1_pcselect));
  Jump_Unit jump_unit_1 (.opcode(rom_1_data[15:12]), .ZF(ZF_q), .CF(CF_q), .jumpOK(jump_unit_1_jumpok));
  or or_1 (or_1_out, control_unit_1_aluand, control_unit_1_aluadd);
  Multiplexer #(.width(16)) multiplexer_2 (
    .in0(ram_1_data), .in1(alu_1_output), .out(multiplexer_2_out), .sel(or_1_out));  // open: en
  Register_File register_file_1 (
    .write_register(rom_1_data[11:8]), .write_value(multiplexer_2_out), .write(control_unit_1_regwrite),
    .clk(clock_1_out), .output1(register_file_1_output1), .read_register1(rom_1_data[7:4]),
    .read_register2(multiplexer_3_out), .output2(register_file_1_output2));
  Multiplexer #(.width(4)) multiplexer_3 (
    .in0(rom_1_data[3:0]), .in1(rom_1_data[11:8]), .out(multiplexer_3_out), .sel(control_unit_1_datamemwrite));  // open: en
  assign bit_extender_1_out = {{12{1'b0}}, multiplexer_3_out};  // Bit_Extender bit_extender_1
  assign bit_extender_2_out = {{12{1'b1}}, multiplexer_3_out};  // Bit_Extender bit_extender_2
  Flag_Unit flag_unit_1 (
    .a(register_file_1_output1), .b(register_file_1_output2), .CF(flag_unit_1_cf), .ZF(flag_unit_1_zf));
  Multiplexer #(.width(16)) multiplexer_4 (
    .in0(bit_extender_1_out), .in1(bit_extender_2_out), .out(multiplexer_4_out), .sel(multiplexer_3_out[3]));  // open: en
  Register #(.width(1)) ZF (
    .D(flag_unit_1_zf), .en(control_unit_1_comparator), .Q(ZF_q), .clk(clock_1_out));  // open: clr
  Multiplexer #(.width(16)) multiplexer_5 (
    .in0(register_file_1_output2), .in1(multiplexer_4_out), .out(multiplexer_5_out),
    .sel(control_unit_1_immediate));  // open: en
  Register #(.width(1)) CF (
    .D(flag_unit_1_cf), .en(control_unit_1_comparator), .Q(CF_q), .clk(clock_1_out));  // open: clr
  assign bit_extender_3_out = {{4{1'b0}}, rom_1_data[7:0]};  // Bit_Extender bit_extender_3
  ALU alu_1 (
    .ALUand(control_unit_1_aluand), .ALUadd(control_unit_1_aluadd), .a(register_file_1_output1),
    .b(multiplexer_5_out), .\output (alu_1_output));
  RAM #(.addrWidth(12), .dataWidth(16), .bus("separate")) ram_1 (
    .addr(bit_extender_3_out), .din(register_file_1_output2), .data(ram_1_data),
    .str(control_unit_1_datamemwrite), .clk(clock_1_out), .ld(control_unit_1_datamemread));  // open: sel, clr

  // Notes on the sheet:
  //   contents of rom_1 (hex, n*v repeats v):
  //   1107 1314 15a6 171b 1912 1b1d 1d19 320d 1204 1808 5103 5205 5301 5406 5507 5604 5907 530a 4603 4a06
  //   4c02 4e00 4104 4007 1446 1540 111f 550d 4703 550d 4703 cff8 550d 4703 550d 4703 bffb 1776 1870 6035
  //   1111 7003 6027 a21 7006 1b2a 6060 1c2b 9ff1 1d2c aff8 1e2d 8003 7ffd 6057 7fcf
endmodule

// H C
module Half_Comparator (
  input  a,
  input  b,
  output gt,
  output eq,
  output lt
);

  wire not_1_out, not_2_out;

  not not_1 (not_1_out, a);
  not not_2 (not_2_out, b);
  and and_1 (gt, a, not_2_out);
  xnor xnor_1 (eq, a, b);
  and and_2 (lt, b, not_1_out);
endmodule

// F C
module Full_Comparator (
  input  a,
  input  b,
  input  gt_in,
  input  eq_in,
  input  lt_in,
  output gt_out,
  output eq_out,
  output lt_out
);

  wire and_1_out, and_2_out, not_1_out, not_2_out, xnor_1_out;

  not not_1 (not_1_out, a);
  not not_2 (not_2_out, b);
  and and_1 (and_1_out, a, eq_in, not_2_out);
  xnor xnor_1 (xnor_1_out, a, b);
  and and_2 (and_2_out, not_1_out, eq_in, b);
  or or_1 (gt_out, and_1_out, gt_in);
  and and_3 (eq_out, xnor_1_out, eq_in);
  or or_2 (lt_out, lt_in, and_2_out);
endmodule

// 4 C
module _4_bit_Comparator (
  input  [3:0] a,
  input  [3:0] b,
  input  gt_in,
  input  eq_in,
  input  lt_in,
  output gt_out,
  output eq_out,
  output lt_out
);

  wire full_comparator_1_eq_out, full_comparator_1_gt_out, full_comparator_1_lt_out,
       full_comparator_2_eq_out, full_comparator_2_gt_out, full_comparator_2_lt_out,
       full_comparator_3_eq_out, full_comparator_3_gt_out, full_comparator_3_lt_out;

  Full_Comparator full_comparator_1 (
    .gt_in(gt_in), .eq_in(eq_in), .lt_in(lt_in), .a(a[3]), .b(b[3]), .gt_out(full_comparator_1_gt_out),
    .eq_out(full_comparator_1_eq_out), .lt_out(full_comparator_1_lt_out));
  Full_Comparator full_comparator_2 (
    .gt_in(full_comparator_3_gt_out), .eq_in(full_comparator_3_eq_out), .lt_in(full_comparator_3_lt_out),
    .a(a[1]), .b(b[1]), .gt_out(full_comparator_2_gt_out), .eq_out(full_comparator_2_eq_out),
    .lt_out(full_comparator_2_lt_out));
  Full_Comparator full_comparator_3 (
    .gt_in(full_comparator_1_gt_out), .eq_in(full_comparator_1_eq_out), .lt_in(full_comparator_1_lt_out),
    .a(a[2]), .b(b[2]), .gt_out(full_comparator_3_gt_out), .eq_out(full_comparator_3_eq_out),
    .lt_out(full_comparator_3_lt_out));
  Full_Comparator full_comparator_4 (
    .gt_in(full_comparator_2_gt_out), .eq_in(full_comparator_2_eq_out), .lt_in(full_comparator_2_lt_out),
    .a(a[0]), .b(b[0]), .gt_out(gt_out), .eq_out(eq_out), .lt_out(lt_out));
endmodule

// 16C
module _16_bit_Comparator (
  input  [15:0] a,
  input  [15:0] b,
  output gt_out,
  output eq_out,
  output ls_out
);

  wire n4_bit_comparator_1_eq_out, n4_bit_comparator_1_gt_out, n4_bit_comparator_1_lt_out,
       n4_bit_comparator_2_eq_out, n4_bit_comparator_2_gt_out, n4_bit_comparator_2_lt_out,
       n4_bit_comparator_3_eq_out, n4_bit_comparator_3_gt_out, n4_bit_comparator_3_lt_out;

  _4_bit_Comparator u_4_bit_comparator_1 (
    .a(a[15:12]), .b(b[15:12]), .gt_in(1'b0), .eq_in(1'b1), .lt_in(1'b0),
    .gt_out(n4_bit_comparator_1_gt_out), .eq_out(n4_bit_comparator_1_eq_out),
    .lt_out(n4_bit_comparator_1_lt_out));
  _4_bit_Comparator u_4_bit_comparator_2 (
    .a(a[11:8]), .b(b[11:8]), .gt_in(n4_bit_comparator_1_gt_out), .eq_in(n4_bit_comparator_1_eq_out),
    .lt_in(n4_bit_comparator_1_lt_out), .gt_out(n4_bit_comparator_2_gt_out),
    .eq_out(n4_bit_comparator_2_eq_out), .lt_out(n4_bit_comparator_2_lt_out));
  _4_bit_Comparator u_4_bit_comparator_3 (
    .a(a[7:4]), .b(b[7:4]), .gt_in(n4_bit_comparator_2_gt_out), .eq_in(n4_bit_comparator_2_eq_out),
    .lt_in(n4_bit_comparator_2_lt_out), .gt_out(n4_bit_comparator_3_gt_out),
    .eq_out(n4_bit_comparator_3_eq_out), .lt_out(n4_bit_comparator_3_lt_out));
  _4_bit_Comparator u_4_bit_comparator_4 (
    .a(a[3:0]), .b(b[3:0]), .gt_in(n4_bit_comparator_3_gt_out), .eq_in(n4_bit_comparator_3_eq_out),
    .lt_in(n4_bit_comparator_3_lt_out), .gt_out(gt_out), .eq_out(eq_out), .lt_out(ls_out));
endmodule

// J U
module Jump_Unit (
  input  [3:0] opcode,
  input  ZF,
  input  CF,
  output jumpOK
);

  wire and_1_out, and_2_out, and_3_out, and_4_out, and_5_out, decoder_1_out7, decoder_1_out8, decoder_1_out9,
       decoder_1_out10, decoder_1_out11, decoder_1_out12, not_1_out, not_2_out, not_3_out, not_4_out,
       not_5_out, or_1_out;

  Decoder #(.select(4)) decoder_1 (
    .out7(decoder_1_out7), .out8(decoder_1_out8), .out9(decoder_1_out9), .out10(decoder_1_out10),
    .out11(decoder_1_out11), .out12(decoder_1_out12), .sel(opcode));  // open: out0, out1, out2, out3, out4, out5, out6, out13, out14, out15, en
  not not_1 (not_1_out, CF);
  not not_2 (not_2_out, ZF);
  not not_3 (not_3_out, CF);
  not not_4 (not_4_out, ZF);
  or or_1 (or_1_out, ZF, CF);
  not not_5 (not_5_out, CF);
  and and_1 (and_1_out, decoder_1_out8, ZF, not_1_out);
  and and_2 (and_2_out, decoder_1_out9, not_2_out, not_3_out);
  and and_3 (and_3_out, decoder_1_out10, not_4_out, CF);
  and and_4 (and_4_out, decoder_1_out11, or_1_out);
  and and_5 (and_5_out, decoder_1_out12, not_5_out);
  or or_2 (jumpOK, decoder_1_out7, and_1_out, and_2_out, and_3_out, and_4_out, and_5_out);
endmodule

// 12 A
module _12_bit_Adder (
  input  [11:0] a,
  input  [11:0] b,
  output [11:0] \output 
);

  wire n4_bit_adder_1_carry_out;

  _4_bit_Adder u_4_bit_adder_1 (
    .a(a[3:0]), .b(b[3:0]), .carry_in(1'b0), .carry_out(n4_bit_adder_1_carry_out), .\output (\output [3:0]));
  _8_bit_Adder u_8_bit_adder_1 (
    .a(a[11:4]), .b(b[11:4]), .carry_in(n4_bit_adder_1_carry_out), .out_5(\output [11:4]));  // open: carry_out
endmodule

// F U
module Flag_Unit (
  input  [15:0] a,
  input  [15:0] b,
  output CF,
  output ZF
);

  wire n16_bit_comparator_1_eq_out, n16_bit_comparator_1_gt_out, n16_bit_comparator_1_ls_out, not_1_out,
       not_2_out, not_3_out;

  _16_bit_Comparator u_16_bit_comparator_1 (
    .a(a), .b(b), .gt_out(n16_bit_comparator_1_gt_out), .eq_out(n16_bit_comparator_1_eq_out),
    .ls_out(n16_bit_comparator_1_ls_out));
  not not_1 (not_1_out, n16_bit_comparator_1_gt_out);
  not not_2 (not_2_out, n16_bit_comparator_1_eq_out);
  not not_3 (not_3_out, n16_bit_comparator_1_ls_out);
  and and_1 (CF, not_1_out, not_2_out, n16_bit_comparator_1_ls_out);
  and and_2 (ZF, not_1_out, n16_bit_comparator_1_eq_out, not_3_out);
endmodule
